// Logisim project basic_gates.circ as structural Verilog
module myNOT (
  input  in_1,
  output out_2
);

  nand nand_1 (out_2, in_1, in_1);
endmodule

module myAND (
  input  in_1,
  input  in_2,
  output out_3
);

  wire nand_1_out;

  nand nand_1 (nand_1_out, in_1, in_2);
  nand nand_2 (out_3, nand_1_out, nand_1_out);
endmodule

module myOR (
  input  in_1,
  input  in_2,
  output out_3
);

  wire nand_1_out, nand_2_out;

  nand nand_1 (nand_1_out, in_1, in_1);
  nand nand_2 (nand_2_out, in_2, in_2);
  nand nand_3 (out_3, nand_1_out, nand_2_out);
endmodule

module myXOR (
  input  in_1,
  input  in_2,
  output out_3
);

  wire nand_1_out, nand_2_out, nand_3_out, nand_4_out;

  nand nand_1 (nand_1_out, in_2, in_2);
  nand nand_2 (nand_2_out, in_1, in_1);
  nand nand_3 (nand_3_out, in_1, nand_1_out);
  nand nand_4 (nand_4_out, nand_2_out, in_2);
  nand nand_5 (out_3, nand_3_out, nand_4_out);
endmodule

module MUX (
  input  in_1,
  input  in_2,
  input  sel,
  output out_4
);

  wire and_1_out, and_2_out, not_1_out;

  not not_1 (not_1_out, sel);
  and and_1 (and_1_out, in_1, not_1_out);
  and and_2 (and_2_out, in_2, sel);
  or or_1 (out_4, and_1_out, and_2_out);
endmodule

module DMUX (
  input  in_1,
  input  sel,
  output out_3,
  output out_4
);

  wire not_1_out;

  not not_1 (not_1_out, sel);
  and and_1 (out_3, in_1, not_1_out);
  and and_2 (out_4, in_1, sel);
endmodule

module nandMUX (
  input  a,
  input  b,
  input  sel,
  output x
);

  wire nand_1_out, nand_2_out, nand_3_out;

  nand nand_1 (nand_1_out, 1'b1, sel);
  nand nand_2 (nand_2_out, a, nand_1_out);
  nand nand_3 (nand_3_out, b, sel);
  nand nand_4 (x, nand_2_out, nand_3_out);
endmodule

module NOT16 (
  input  in_1,
  input  in_2,
  input  in_3,
  input  in_4,
  input  in_5,
  input  in_6,
  input  in_7,
  input  in_8,
  input  in_9,
  input  in_10,
  input  in_11,
  input  in_12,
  input  in_13,
  input  in_14,
  input  in_15,
  input  in_16,
  output out_17,
  output out_18,
  output out_19,
  output out_20,
  output out_21,
  output out_22,
  output out_23,
  output out_24,
  output out_25,
  output out_26,
  output out_27,
  output out_28,
  output out_29,
  output out_30,
  output out_31,
  output out_32
);

  nand nand_1 (out_17, in_1, in_1);
  nand nand_2 (out_18, in_2, in_2);
  nand nand_3 (out_19, in_3, in_3);
  nand nand_4 (out_20, in_4, in_4);
  nand nand_5 (out_21, in_5, in_5);
  nand nand_6 (out_22, in_6, in_6);
  nand nand_7 (out_23, in_7, in_7);
  nand nand_8 (out_24, in_8, in_8);
  nand nand_9 (out_25, in_9, in_9);
  nand nand_10 (out_26, in_10, in_10);
  nand nand_11 (out_27, in_11, in_11);
  nand nand_12 (out_28, in_12, in_12);
  nand nand_13 (out_29, in_13, in_13);
  nand nand_14 (out_30, in_14, in_14);
  nand nand_15 (out_31, in_15, in_15);
  nand nand_16 (out_32, in_16, in_16);
endmodule

module AND16 (
  input  in_1,
  input  in_2,
  input  in_3,
  input  in_4,
  input  in_5,
  input  in_6,
  input  in_7,
  input  in_8,
  input  in_9,
  input  in_10,
  input  in_11,
  input  in_12,
  input  in_13,
  input  in_14,
  input  in_15,
  input  in_16,
  input  in_17,
  input  in_18,
  input  in_19,
  input  in_20,
  input  in_21,
  input  in_22,
  input  in_23,
  input  in_24,
  input  in_25,
  input  in_26,
  input  in_27,
  input  in_28,
  input  in_29,
  input  in_30,
  input  in_31,
  input  in_32,
  output out_33,
  output out_34,
  output out_35,
  output out_36,
  output out_37,
  output out_38,
  output out_39,
  output out_40,
  output out_41,
  output out_42,
  output out_43,
  output out_44,
  output out_45,
  output out_46,
  output out_47,
  output out_48
);

  wire nand_1_out, nand_2_out, nand_3_out, nand_4_out, nand_5_out, nand_6_out, nand_7_out, nand_8_out,
       nand_9_out, nand_10_out, nand_11_out, nand_12_out, nand_13_out, nand_14_out, nand_15_out, nand_16_out;

  nand nand_1 (nand_1_out, in_1, in_2);
  nand nand_2 (nand_2_out, in_3, in_4);
  nand nand_3 (nand_3_out, in_5, in_6);
  nand nand_4 (nand_4_out, in_7, in_8);
  nand nand_5 (nand_5_out, in_9, in_10);
  nand nand_6 (nand_6_out, in_11, in_12);
  nand nand_7 (nand_7_out, in_13, in_14);
  nand nand_8 (nand_8_out, in_15, in_16);
  nand nand_9 (nand_9_out, in_17, in_18);
  nand nand_10 (nand_10_out, in_19, in_20);
  nand nand_11 (nand_11_out, in_21, in_22);
  nand nand_12 (nand_12_out, in_23, in_24);
  nand nand_13 (nand_13_out, in_25, in_26);
  nand nand_14 (nand_14_out, in_27, in_28);
  nand nand_15 (nand_15_out, in_29, in_30);
  nand nand_16 (nand_16_out, in_31, in_32);
  nand nand_17 (out_33, nand_1_out, nand_1_out);
  nand nand_18 (out_34, nand_2_out, nand_2_out);
  nand nand_19 (out_35, nand_3_out, nand_3_out);
  nand nand_20 (out_36, nand_4_out, nand_4_out);
  nand nand_21 (out_37, nand_5_out, nand_5_out);
  nand nand_22 (out_38, nand_6_out, nand_6_out);
  nand nand_23 (out_39, nand_7_out, nand_7_out);
  nand nand_24 (out_40, nand_8_out, nand_8_out);
  nand nand_25 (out_41, nand_9_out, nand_9_out);
  nand nand_26 (out_42, nand_10_out, nand_10_out);
  nand nand_27 (out_43, nand_11_out, nand_11_out);
  nand nand_28 (out_44, nand_12_out, nand_12_out);
  nand nand_29 (out_45, nand_13_out, nand_13_out);
  nand nand_30 (out_46, nand_14_out, nand_14_out);
  nand nand_31 (out_47, nand_15_out, nand_15_out);
  nand nand_32 (out_48, nand_16_out, nand_16_out);
endmodule

module OR16 (
  input  in_1,
  input  in_2,
  input  in_3,
  input  in_4,
  input  in_5,
  input  in_6,
  input  in_7,
  input  in_8,
  input  in_9,
  input  in_10,
  input  in_11,
  input  in_12,
  input  in_13,
  input  in_14,
  input  in_15,
  input  in_16,
  input  in_17,
  input  in_18,
  input  in_19,
  input  in_20,
  input  in_21,
  input  in_22,
  input  in_23,
  input  in_24,
  input  in_25,
  input  in_26,
  input  in_27,
  input  in_28,
  input  in_29,
  input  in_30,
  input  in_31,
  input  in_32,
  output out_33,
  output out_34,
  output out_35,
  output out_36,
  output out_37,
  output out_38,
  output out_39,
  output out_40,
  output out_41,
  output out_42,
  output out_43,
  output out_44,
  output out_45,
  output out_46,
  output out_47,
  output out_48
);

  wire nand_1_out, nand_2_out, nand_3_out, nand_4_out, nand_5_out, nand_6_out, nand_7_out, nand_8_out,
       nand_9_out, nand_10_out, nand_11_out, nand_12_out, nand_13_out, nand_14_out, nand_15_out, nand_16_out,
       nand_17_out, nand_18_out, nand_19_out, nand_20_out, nand_21_out, nand_22_out, nand_23_out,
       nand_24_out, nand_25_out, nand_26_out, nand_27_out, nand_28_out, nand_29_out, nand_30_out,
       nand_31_out, nand_32_out;

  nand nand_1 (nand_1_out, in_1, in_1);
  nand nand_2 (nand_2_out, in_2, in_2);
  nand nand_3 (nand_3_out, in_3, in_3);
  nand nand_4 (nand_4_out, in_4, in_4);
  nand nand_5 (nand_5_out, in_5, in_5);
  nand nand_6 (nand_6_out, in_6, in_6);
  nand nand_7 (nand_7_out, in_7, in_7);
  nand nand_8 (nand_8_out, in_8, in_8);
  nand nand_9 (nand_9_out, in_9, in_9);
  nand nand_10 (nand_10_out, in_10, in_10);
  nand nand_11 (nand_11_out, in_11, in_11);
  nand nand_12 (nand_12_out, in_12, in_12);
  nand nand_13 (nand_13_out, in_13, in_13);
  nand nand_14 (nand_14_out, in_14, in_14);
  nand nand_15 (nand_15_out, in_15, in_15);
  nand nand_16 (nand_16_out, in_16, in_16);
  nand nand_17 (nand_17_out, in_17, in_17);
  nand nand_18 (nand_18_out, in_18, in_18);
  nand nand_19 (nand_19_out, in_19, in_19);
  nand nand_20 (nand_20_out, in_20, in_20);
  nand nand_21 (nand_21_out, in_21, in_21);
  nand nand_22 (nand_22_out, in_22, in_22);
  nand nand_23 (nand_23_out, in_23, in_23);
  nand nand_24 (nand_24_out, in_24, in_24);
  nand nand_25 (nand_25_out, in_25, in_25);
  nand nand_26 (nand_26_out, in_26, in_26);
  nand nand_27 (nand_27_out, in_27, in_27);
  nand nand_28 (nand_28_out, in_28, in_28);
  nand nand_29 (nand_29_out, in_29, in_29);
  nand nand_30 (nand_30_out, in_30, in_30);
  nand nand_31 (nand_31_out, in_31, in_31);
  nand nand_32 (nand_32_out, in_32, in_32);
  nand nand_33 (out_33, nand_1_out, nand_2_out);
  nand nand_34 (out_34, nand_3_out, nand_4_out);
  nand nand_35 (out_35, nand_5_out, nand_6_out);
  nand nand_36 (out_36, nand_7_out, nand_8_out);
  nand nand_37 (out_37, nand_9_out, nand_10_out);
  nand nand_38 (out_38, nand_11_out, nand_12_out);
  nand nand_39 (out_39, nand_13_out, nand_14_out);
  nand nand_40 (out_40, nand_15_out, nand_16_out);
  nand nand_41 (out_41, nand_17_out, nand_18_out);
  nand nand_42 (out_42, nand_19_out, nand_20_out);
  nand nand_43 (out_43, nand_21_out, nand_22_out);
  nand nand_44 (out_44, nand_23_out, nand_24_out);
  nand nand_45 (out_45, nand_25_out, nand_26_out);
  nand nand_46 (out_46, nand_27_out, nand_28_out);
  nand nand_47 (out_47, nand_29_out, nand_30_out);
  nand nand_48 (out_48, nand_31_out, nand_32_out);
endmodule

module MUX16 (
  input  sel,
  input  in_2,
  input  in_3,
  input  in_4,
  input  in_5,
  input  in_6,
  input  in_7,
  input  in_8,
  input  in_9,
  input  in_10,
  input  in_11,
  input  in_12,
  input  in_13,
  input  in_14,
  input  in_15,
  input  in_16,
  input  in_17,
  input  in_18,
  input  in_19,
  input  in_20,
  input  in_21,
  input  in_22,
  input  in_23,
  input  in_24,
  input  in_25,
  input  in_26,
  input  in_27,
  input  in_28,
  input  in_29,
  input  in_30,
  input  in_31,
  input  in_32,
  input  in_33,
  output out_34,
  output out_35,
  output out_36,
  output out_37,
  output out_38,
  output out_39,
  output out_40,
  output out_41,
  output out_42,
  output out_43,
  output out_44,
  output out_45,
  output out_46,
  output out_47,
  output out_48,
  output out_49
);

  wire and_1_out, and_2_out, and_3_out, and_4_out, and_5_out, and_6_out, and_7_out, and_8_out, and_9_out,
       and_10_out, and_11_out, and_12_out, and_13_out, and_14_out, and_15_out, and_16_out, and_17_out,
       and_18_out, and_19_out, and_20_out, and_21_out, and_22_out, and_23_out, and_24_out, and_25_out,
       and_26_out, and_27_out, and_28_out, and_29_out, and_30_out, and_31_out, and_32_out, not_1_out,
       not_2_out, not_3_out, not_4_out, not_5_out, not_6_out, not_7_out, not_8_out, not_9_out, not_10_out,
       not_11_out, not_12_out, not_13_out, not_14_out, not_15_out, not_16_out;

  and and_1 (and_1_out, in_2, not_1_out);
  not not_1 (not_1_out, sel);
  and and_2 (and_2_out, in_3, sel);
  and and_3 (and_3_out, in_4, not_2_out);
  not not_2 (not_2_out, sel);
  and and_4 (and_4_out, in_5, sel);
  and and_5 (and_5_out, in_6, not_3_out);
  not not_3 (not_3_out, sel);
  and and_6 (and_6_out, in_7, sel);
  and and_7 (and_7_out, in_8, not_4_out);
  not not_4 (not_4_out, sel);
  and and_8 (and_8_out, in_9, sel);
  and and_9 (and_9_out, in_10, not_5_out);
  not not_5 (not_5_out, sel);
  and and_10 (and_10_out, in_11, sel);
  and and_11 (and_11_out, in_12, not_6_out);
  not not_6 (not_6_out, sel);
  and and_12 (and_12_out, in_13, sel);
  and and_13 (and_13_out, in_14, not_7_out);
  not not_7 (not_7_out, sel);
  and and_14 (and_14_out, in_15, sel);
  and and_15 (and_15_out, in_16, not_8_out);
  not not_8 (not_8_out, sel);
  and and_16 (and_16_out, in_17, sel);
  and and_17 (and_17_out, in_18, not_9_out);
  not not_9 (not_9_out, sel);
  and and_18 (and_18_out, in_19, sel);
  and and_19 (and_19_out, in_20, not_10_out);
  not not_10 (not_10_out, sel);
  and and_20 (and_20_out, in_21, sel);
  and and_21 (and_21_out, in_22, not_11_out);
  not not_11 (not_11_out, sel);
  and and_22 (and_22_out, in_23, sel);
  and and_23 (and_23_out, in_24, not_12_out);
  not not_12 (not_12_out, sel);
  and and_24 (and_24_out, in_25, sel);
  and and_25 (and_25_out, in_26, not_13_out);
  not not_13 (not_13_out, sel);
  and and_26 (and_26_out, in_27, sel);
  and and_27 (and_27_out, in_28, not_14_out);
  not not_14 (not_14_out, sel);
  and and_28 (and_28_out, in_29, sel);
  and and_29 (and_29_out, in_30, not_15_out);
  not not_15 (not_15_out, sel);
  and and_30 (and_30_out, in_31, sel);
  and and_31 (and_31_out, in_32, not_16_out);
  not not_16 (not_16_out, sel);
  and and_32 (and_32_out, in_33, sel);
  or or_1 (out_34, and_1_out, and_2_out);
  or or_2 (out_35, and_3_out, and_4_out);
  or or_3 (out_36, and_5_out, and_6_out);
  or or_4 (out_37, and_7_out, and_8_out);
  or or_5 (out_38, and_9_out, and_10_out);
  or or_6 (out_39, and_11_out, and_12_out);
  or or_7 (out_40, and_13_out, and_14_out);
  or or_8 (out_41, and_15_out, and_16_out);
  or or_9 (out_42, and_17_out, and_18_out);
  or or_10 (out_43, and_19_out, and_20_out);
  or or_11 (out_44, and_21_out, and_22_out);
  or or_12 (out_45, and_23_out, and_24_out);
  or or_13 (out_46, and_25_out, and_26_out);
  or or_14 (out_47, and_27_out, and_28_out);
  or or_15 (out_48, and_29_out, and_30_out);
  or or_16 (out_49, and_31_out, and_32_out);
endmodule

module OR8Way (
  input  in_1,
  input  in_2,
  input  in_3,
  input  in_4,
  input  in_5,
  input  in_6,
  input  in_7,
  input  in_8,
  output out_9
);

  wire nand_1_out, nand_2_out, nand_3_out, nand_4_out, nand_5_out, nand_6_out, nand_7_out, nand_8_out,
       nand_9_out, nand_10_out, nand_11_out, nand_12_out, nand_13_out, nand_14_out, nand_15_out, nand_16_out,
       nand_17_out, nand_18_out, nand_19_out, nand_20_out;

  nand nand_1 (nand_1_out, in_1, in_1);
  nand nand_2 (nand_2_out, in_2, in_2);
  nand nand_3 (nand_3_out, in_3, in_3);
  nand nand_4 (nand_4_out, in_4, in_4);
  nand nand_5 (nand_5_out, in_5, in_5);
  nand nand_6 (nand_6_out, in_6, in_6);
  nand nand_7 (nand_7_out, in_7, in_7);
  nand nand_8 (nand_8_out, in_8, in_8);
  nand nand_9 (nand_9_out, nand_1_out, nand_2_out);
  nand nand_10 (nand_10_out, nand_3_out, nand_4_out);
  nand nand_11 (nand_11_out, nand_5_out, nand_6_out);
  nand nand_12 (nand_12_out, nand_7_out, nand_8_out);
  nand nand_13 (nand_13_out, nand_9_out, nand_9_out);
  nand nand_14 (nand_14_out, nand_10_out, nand_10_out);
  nand nand_15 (nand_15_out, nand_11_out, nand_11_out);
  nand nand_16 (nand_16_out, nand_12_out, nand_12_out);
  nand nand_17 (nand_17_out, nand_13_out, nand_14_out);
  nand nand_18 (nand_18_out, nand_15_out, nand_16_out);
  nand nand_19 (nand_19_out, nand_17_out, nand_17_out);
  nand nand_20 (nand_20_out, nand_18_out, nand_18_out);
  nand nand_21 (out_9, nand_19_out, nand_20_out);
endmodule

module MUX4Way16 (
  input  in_1,
  input  sel1,
  input  sel2,
  input  in_4,
  input  in_5,
  input  in_6,
  input  in_7,
  input  in_8,
  input  in_9,
  input  in_10,
  input  in_11,
  input  in_12,
  input  in_13,
  input  in_14,
  input  in_15,
  input  in_16,
  input  in_17,
  input  in_18,
  input  in_19,
  input  in_20,
  input  in_21,
  input  in_22,
  input  in_23,
  input  in_24,
  input  in_25,
  input  in_26,
  input  in_27,
  input  in_28,
  input  in_29,
  input  in_30,
  input  in_31,
  input  in_32,
  input  in_33,
  input  in_34,
  input  in_35,
  input  in_36,
  input  in_37,
  input  in_38,
  input  in_39,
  input  in_40,
  input  in_41,
  input  in_42,
  input  in_43,
  input  in_44,
  input  in_45,
  input  in_46,
  input  in_47,
  input  in_48,
  input  in_49,
  input  in_50,
  input  in_51,
  input  in_52,
  input  in_53,
  input  in_54,
  input  in_55,
  input  in_56,
  input  in_57,
  input  in_58,
  input  in_59,
  input  in_60,
  input  in_61,
  input  in_62,
  input  in_63,
  input  in_64,
  input  in_65,
  input  in_66,
  output out_67,
  output out_68,
  output out_69,
  output out_70,
  output out_71,
  output out_72,
  output out_73,
  output out_74,
  output out_75,
  output out_76,
  output out_77,
  output out_78,
  output out_79,
  output out_80,
  output out_81,
  output out_82
);

  wire and_1_out, and_2_out, and_3_out, and_4_out, and_5_out, and_6_out, and_7_out, and_8_out, and_9_out,
       and_10_out, and_11_out, and_12_out, and_13_out, and_14_out, and_15_out, and_16_out, and_17_out,
       and_18_out, and_19_out, and_20_out, and_21_out, and_22_out, and_23_out, and_24_out, and_25_out,
       and_26_out, and_27_out, and_28_out, and_29_out, and_30_out, and_31_out, and_32_out, and_33_out,
       and_34_out, and_35_out, and_36_out, and_37_out, and_38_out, and_39_out, and_40_out, and_41_out,
       and_42_out, and_43_out, and_44_out, and_45_out, and_46_out, and_47_out, and_48_out, and_49_out,
       and_50_out, and_51_out, and_52_out, and_53_out, and_54_out, and_55_out, and_56_out, and_57_out,
       and_58_out, and_59_out, and_60_out, and_61_out, and_62_out, and_63_out, and_64_out, and_65_out,
       and_66_out, and_67_out, and_68_out, not_1_out, not_2_out, or_1_out, or_2_out, or_3_out, or_4_out,
       or_5_out, or_6_out, or_7_out, or_8_out, or_9_out, or_10_out, or_11_out, or_12_out, or_13_out,
       or_14_out, or_15_out, or_16_out, or_17_out, or_18_out, or_19_out, or_20_out, or_21_out, or_22_out,
       or_23_out, or_24_out, or_25_out, or_26_out, or_27_out, or_28_out, or_29_out, or_30_out, or_31_out,
       or_32_out;

  not not_1 (not_1_out, sel1);
  not not_2 (not_2_out, sel2);
  and and_1 (and_1_out, not_1_out, not_2_out);
  and and_2 (and_2_out, not_1_out, sel2);
  and and_3 (and_3_out, sel1, not_2_out);
  and and_4 (and_4_out, sel1, sel2);
  and and_5 (and_5_out, in_1, and_1_out);
  and and_6 (and_6_out, in_4, and_2_out);
  and and_7 (and_7_out, in_5, and_3_out);
  and and_8 (and_8_out, in_6, and_4_out);
  and and_9 (and_9_out, in_7, and_1_out);
  and and_10 (and_10_out, in_8, and_2_out);
  and and_11 (and_11_out, in_9, and_3_out);
  and and_12 (and_12_out, in_10, and_4_out);
  and and_13 (and_13_out, in_11, and_1_out);
  and and_14 (and_14_out, in_12, and_2_out);
  and and_15 (and_15_out, in_13, and_3_out);
  and and_16 (and_16_out, in_14, and_4_out);
  and and_17 (and_17_out, in_15, and_1_out);
  and and_18 (and_18_out, in_16, and_2_out);
  and and_19 (and_19_out, in_17, and_3_out);
  and and_20 (and_20_out, in_18, and_4_out);
  and and_21 (and_21_out, in_19, and_1_out);
  and and_22 (and_22_out, in_20, and_2_out);
  and and_23 (and_23_out, in_21, and_3_out);
  and and_24 (and_24_out, in_22, and_4_out);
  and and_25 (and_25_out, in_23, and_1_out);
  and and_26 (and_26_out, in_24, and_2_out);
  and and_27 (and_27_out, in_25, and_3_out);
  and and_28 (and_28_out, in_26, and_4_out);
  and and_29 (and_29_out, in_27, and_1_out);
  and and_30 (and_30_out, in_28, and_2_out);
  and and_31 (and_31_out, in_29, and_3_out);
  and and_32 (and_32_out, in_30, and_4_out);
  and and_33 (and_33_out, in_31, and_1_out);
  and and_34 (and_34_out, in_32, and_2_out);
  and and_35 (and_35_out, in_33, and_3_out);
  and and_36 (and_36_out, in_34, and_4_out);
  and and_37 (and_37_out, in_35, and_1_out);
  and and_38 (and_38_out, in_36, and_2_out);
  and and_39 (and_39_out, in_37, and_3_out);
  and and_40 (and_40_out, in_38, and_4_out);
  and and_41 (and_41_out, in_39, and_1_out);
  and and_42 (and_42_out, in_40, and_2_out);
  and and_43 (and_43_out, in_41, and_3_out);
  and and_44 (and_44_out, in_42, and_4_out);
  and and_45 (and_45_out, in_43, and_1_out);
  and and_46 (and_46_out, in_44, and_2_out);
  and and_47 (and_47_out, in_45, and_3_out);
  and and_48 (and_48_out, in_46, and_4_out);
  and and_49 (and_49_out, in_47, and_1_out);
  and and_50 (and_50_out, in_48, and_2_out);
  and and_51 (and_51_out, in_49, and_3_out);
  and and_52 (and_52_out, in_50, and_4_out);
  and and_53 (and_53_out, in_51, and_1_out);
  and and_54 (and_54_out, in_52, and_2_out);
  and and_55 (and_55_out, in_53, and_3_out);
  and and_56 (and_56_out, in_54, and_4_out);
  and and_57 (and_57_out, in_55, and_1_out);
  and and_58 (and_58_out, in_56, and_2_out);
  and and_59 (and_59_out, in_57, and_3_out);
  and and_60 (and_60_out, in_58, and_4_out);
  and and_61 (and_61_out, in_59, and_1_out);
  and and_62 (and_62_out, in_60, and_2_out);
  and and_63 (and_63_out, in_61, and_3_out);
  and and_64 (and_64_out, in_62, and_4_out);
  and and_65 (and_65_out, in_63, and_1_out);
  and and_66 (and_66_out, in_64, and_2_out);
  and and_67 (and_67_out, in_65, and_3_out);
  and and_68 (and_68_out, in_66, and_4_out);
  or or_1 (or_1_out, and_5_out, and_6_out);
  or or_2 (or_2_out, and_7_out, and_8_out);
  or or_3 (or_3_out, and_9_out, and_10_out);
  or or_4 (or_4_out, and_11_out, and_12_out);
  or or_5 (or_5_out, and_13_out, and_14_out);
  or or_6 (or_6_out, and_15_out, and_16_out);
  or or_7 (or_7_out, and_17_out, and_18_out);
  or or_8 (or_8_out, and_19_out, and_20_out);
  or or_9 (or_9_out, and_21_out, and_22_out);
  or or_10 (or_10_out, and_23_out, and_24_out);
  or or_11 (or_11_out, and_25_out, and_26_out);
  or or_12 (or_12_out, and_27_out, and_28_out);
  or or_13 (or_13_out, and_29_out, and_30_out);
  or or_14 (or_14_out, and_31_out, and_32_out);
  or or_15 (or_15_out, and_33_out, and_34_out);
  or or_16 (or_16_out, and_35_out, and_36_out);
  or or_17 (or_17_out, and_37_out, and_38_out);
  or or_18 (or_18_out, and_39_out, and_40_out);
  or or_19 (or_19_out, and_41_out, and_42_out);
  or or_20 (or_20_out, and_43_out, and_44_out);
  or or_21 (or_21_out, and_45_out, and_46_out);
  or or_22 (or_22_out, and_47_out, and_48_out);
  or or_23 (or_23_out, and_49_out, and_50_out);
  or or_24 (or_24_out, and_51_out, and_52_out);
  or or_25 (or_25_out, and_53_out, and_54_out);
  or or_26 (or_26_out, and_55_out, and_56_out);
  or or_27 (or_27_out, and_57_out, and_58_out);
  or or_28 (or_28_out, and_59_out, and_60_out);
  or or_29 (or_29_out, and_61_out, and_62_out);
  or or_30 (or_30_out, and_63_out, and_64_out);
  or or_31 (or_31_out, and_65_out, and_66_out);
  or or_32 (or_32_out, and_67_out, and_68_out);
  or or_33 (out_67, or_1_out, or_2_out);
  or or_34 (out_68, or_3_out, or_4_out);
  or or_35 (out_69, or_5_out, or_6_out);
  or or_36 (out_70, or_7_out, or_8_out);
  or or_37 (out_71, or_9_out, or_10_out);
  or or_38 (out_72, or_11_out, or_12_out);
  or or_39 (out_73, or_13_out, or_14_out);
  or or_40 (out_74, or_15_out, or_16_out);
  or or_41 (out_75, or_17_out, or_18_out);
  or or_42 (out_76, or_19_out, or_20_out);
  or or_43 (out_77, or_21_out, or_22_out);
  or or_44 (out_78, or_23_out, or_24_out);
  or or_45 (out_79, or_25_out, or_26_out);
  or or_46 (out_80, or_27_out, or_28_out);
  or or_47 (out_81, or_29_out, or_30_out);
  or or_48 (out_82, or_31_out, or_32_out);
endmodule

module MUX8Way16 (
  input  [15:0] in_1,
  input  [15:0] in_2,
  input  [15:0] in_3,
  input  [15:0] in_4,
  input  in_5,
  input  in_6,
  input  in_7,
  input  [15:0] in_8,
  input  [15:0] in_9,
  input  [15:0] in_10,
  input  [15:0] in_11,
  output [15:0] out_12
);

  wire [15:0] multiplexer_1_out, multiplexer_2_out;

  Multiplexer #(.select(2), .width(16)) multiplexer_1 (
    .in0(in_1), .in1(in_2), .in2(in_3), .in3(in_4), .out(multiplexer_1_out), .sel({in_6, in_7}));
  Multiplexer #(.select(2), .width(16)) multiplexer_2 (
    .in0(in_8), .in1(in_9), .in2(in_10), .in3(in_11), .out(multiplexer_2_out), .sel({in_6, in_7}));
  Multiplexer #(.width(16)) multiplexer_3 (.in0(multiplexer_1_out), .in1(multiplexer_2_out), .out(out_12), .sel(in_5));
endmodule
