// Logisim project bool_arithmetic.circ as structural Verilog: 11 circuits, main circuit HalfAdder
module HalfAdder (
  input  a,
  input  b,
  output sum,
  output carry
);

  xor xor_1 (sum, a, b);
  and and_1 (carry, a, b);
endmodule

module FullAdder (
  input  a,
  input  b,
  input  c,
  output sum,
  output carry
);

  wire and_1_out, and_2_out, xor_1_out;

  xor xor_1 (xor_1_out, a, b);
  xor xor_2 (sum, xor_1_out, c);
  and and_1 (and_1_out, xor_1_out, c);
  and and_2 (and_2_out, a, b);
  or or_1 (carry, and_1_out, and_2_out);
endmodule

module FullAdderC (
  input  in_1,
  input  in_2,
  input  in_3,
  output out_4,
  output out_5
);

  wire halfadder_1_carry, halfadder_1_sum, halfadder_2_carry;

  HalfAdder halfadder_1 (.a(in_1), .b(in_2), .sum(halfadder_1_sum), .carry(halfadder_1_carry));
  HalfAdder halfadder_2 (.a(halfadder_1_sum), .b(in_3), .sum(out_5), .carry(halfadder_2_carry));
  or or_1 (out_4, halfadder_1_carry, halfadder_2_carry);
endmodule

module FullAdderTTL (
  input  c,
  input  a,
  input  b,
  output carry,
  output sum
);

  wire n7408_1_pin3, n7408_1_pin6, n7486_1_pin7, n7486_1_pin11, n7486_1_pin14;

  _7486 #(.ShowInternalStructure("true"), .VccGndPorts("true")) u_7486_1 (
    .pin7(n7486_1_pin7), .pin14(n7486_1_pin14), .pin13(b), .pin12(a), .pin11(n7486_1_pin11),
    .pin10(n7486_1_pin11), .pin9(c), .pin8(sum));  // open: pin1, pin2, pin3, pin4, pin5, pin6
  _7408 #(.ShowInternalStructure("true"), .VccGndPorts("true")) u_7408_1 (
    .pin1(n7486_1_pin11), .pin2(c), .pin3(n7408_1_pin3), .pin4(a), .pin5(b), .pin6(n7408_1_pin6),
    .pin7(n7486_1_pin7), .pin14(n7486_1_pin14));  // open: pin13, pin12, pin11, pin10, pin9, pin8
  _7432 #(.ShowInternalStructure("true"), .VccGndPorts("true")) u_7432_1 (
    .pin1(n7408_1_pin3), .pin2(n7408_1_pin6), .pin3(carry), .pin7(n7486_1_pin7), .pin14(n7486_1_pin14));  // open: pin4, pin5, pin6, pin13, pin12, pin11, pin10, pin9, pin8
  // also tied to GND on the sheet: n7486_1_pin7
  // also tied to VCC on the sheet: n7486_1_pin14
endmodule

module Add16 (
  input  c,
  input  [15:0] a,
  input  [15:0] b,
  output [15:0] sum
);

  wire and_1_out, and_2_out, and_3_out, and_4_out, and_5_out, and_6_out, and_7_out, and_8_out, and_9_out,
       and_10_out, and_11_out, and_12_out, and_13_out, and_14_out, and_15_out, and_16_out, and_17_out,
       and_18_out, and_19_out, and_20_out, and_21_out, and_22_out, and_23_out, and_24_out, and_25_out,
       and_26_out, and_27_out, and_28_out, and_29_out, and_30_out, and_31_out, and_32_out, or_1_out,
       or_2_out, or_3_out, or_4_out, or_5_out, or_6_out, or_7_out, or_8_out, or_9_out, or_10_out, or_11_out,
       or_12_out, or_13_out, or_14_out, or_15_out, or_16_out, xor_1_out, xor_2_out, xor_3_out, xor_4_out,
       xor_5_out, xor_6_out, xor_7_out, xor_8_out, xor_9_out, xor_10_out, xor_11_out, xor_12_out, xor_13_out,
       xor_14_out, xor_15_out, xor_16_out;

  xor xor_1 (xor_1_out, a[0], b[0]);
  xor xor_2 (xor_2_out, a[1], b[1]);
  xor xor_3 (xor_3_out, a[2], b[2]);
  xor xor_4 (xor_4_out, a[3], b[3]);
  xor xor_5 (xor_5_out, a[4], b[4]);
  xor xor_6 (xor_6_out, a[5], b[5]);
  xor xor_7 (xor_7_out, a[6], b[6]);
  xor xor_8 (xor_8_out, a[7], b[7]);
  xor xor_9 (xor_9_out, a[8], b[8]);
  xor xor_10 (xor_10_out, a[9], b[9]);
  xor xor_11 (xor_11_out, a[10], b[10]);
  xor xor_12 (xor_12_out, a[11], b[11]);
  xor xor_13 (xor_13_out, a[12], b[12]);
  xor xor_14 (xor_14_out, a[13], b[13]);
  xor xor_15 (xor_15_out, a[14], b[14]);
  xor xor_16 (xor_16_out, a[15], b[15]);
  xor xor_17 (sum[0], xor_1_out, c);
  and and_1 (and_1_out, xor_1_out, c);
  and and_2 (and_2_out, a[0], b[0]);
  xor xor_18 (sum[1], xor_2_out, or_1_out);
  and and_3 (and_3_out, xor_2_out, or_1_out);
  and and_4 (and_4_out, a[1], b[1]);
  xor xor_19 (sum[2], xor_3_out, or_2_out);
  and and_5 (and_5_out, xor_3_out, or_2_out);
  and and_6 (and_6_out, a[2], b[2]);
  xor xor_20 (sum[3], xor_4_out, or_3_out);
  and and_7 (and_7_out, xor_4_out, or_3_out);
  and and_8 (and_8_out, a[3], b[3]);
  xor xor_21 (sum[4], xor_5_out, or_4_out);
  and and_9 (and_9_out, xor_5_out, or_4_out);
  and and_10 (and_10_out, a[4], b[4]);
  xor xor_22 (sum[5], xor_6_out, or_5_out);
  and and_11 (and_11_out, xor_6_out, or_5_out);
  and and_12 (and_12_out, a[5], b[5]);
  xor xor_23 (sum[6], xor_7_out, or_6_out);
  and and_13 (and_13_out, xor_7_out, or_6_out);
  and and_14 (and_14_out, a[6], b[6]);
  xor xor_24 (sum[7], xor_8_out, or_7_out);
  and and_15 (and_15_out, xor_8_out, or_7_out);
  and and_16 (and_16_out, a[7], b[7]);
  xor xor_25 (sum[8], xor_9_out, or_8_out);
  and and_17 (and_17_out, xor_9_out, or_8_out);
  and and_18 (and_18_out, a[8], b[8]);
  xor xor_26 (sum[9], xor_10_out, or_9_out);
  and and_19 (and_19_out, xor_10_out, or_9_out);
  and and_20 (and_20_out, a[9], b[9]);
  xor xor_27 (sum[10], xor_11_out, or_10_out);
  and and_21 (and_21_out, xor_11_out, or_10_out);
  and and_22 (and_22_out, a[10], b[10]);
  xor xor_28 (sum[11], xor_12_out, or_11_out);
  and and_23 (and_23_out, xor_12_out, or_11_out);
  and and_24 (and_24_out, a[11], b[11]);
  xor xor_29 (sum[12], xor_13_out, or_12_out);
  and and_25 (and_25_out, xor_13_out, or_12_out);
  and and_26 (and_26_out, a[12], b[12]);
  xor xor_30 (sum[13], xor_14_out, or_13_out);
  and and_27 (and_27_out, xor_14_out, or_13_out);
  and and_28 (and_28_out, a[13], b[13]);
  xor xor_31 (sum[14], xor_15_out, or_14_out);
  and and_29 (and_29_out, xor_15_out, or_14_out);
  and and_30 (and_30_out, a[14], b[14]);
  xor xor_32 (sum[15], xor_16_out, or_15_out);
  and and_31 (and_31_out, xor_16_out, or_15_out);
  and and_32 (and_32_out, a[15], b[15]);
  or or_1 (or_1_out, and_1_out, and_2_out);
  or or_2 (or_2_out, and_3_out, and_4_out);
  or or_3 (or_3_out, and_5_out, and_6_out);
  or or_4 (or_4_out, and_7_out, and_8_out);
  or or_5 (or_5_out, and_9_out, and_10_out);
  or or_6 (or_6_out, and_11_out, and_12_out);
  or or_7 (or_7_out, and_13_out, and_14_out);
  or or_8 (or_8_out, and_15_out, and_16_out);
  or or_9 (or_9_out, and_17_out, and_18_out);
  or or_10 (or_10_out, and_19_out, and_20_out);
  or or_11 (or_11_out, and_21_out, and_22_out);
  or or_12 (or_12_out, and_23_out, and_24_out);
  or or_13 (or_13_out, and_25_out, and_26_out);
  or or_14 (or_14_out, and_27_out, and_28_out);
  or or_15 (or_15_out, and_29_out, and_30_out);
  or or_16 (or_16_out, and_31_out, and_32_out);
endmodule

module Add16C (
  input  [15:0] a,
  input  [15:0] b,
  output [15:0] out_3
);

  wire fulladder_1_carry, fulladder_2_carry, fulladder_3_carry, fulladder_4_carry, fulladder_5_carry,
       fulladder_6_carry, fulladder_7_carry, fulladder_8_carry, fulladder_9_carry, fulladder_10_carry,
       fulladder_11_carry, fulladder_12_carry, fulladder_13_carry, fulladder_14_carry, fulladder_15_carry;

  FullAdder fulladder_1 (.a(a[0]), .b(b[0]), .sum(out_3[0]), .carry(fulladder_1_carry));  // open: c
  FullAdder fulladder_2 (.a(a[1]), .b(b[1]), .c(fulladder_1_carry), .sum(out_3[1]), .carry(fulladder_2_carry));
  FullAdder fulladder_3 (.a(a[2]), .b(b[2]), .c(fulladder_2_carry), .sum(out_3[2]), .carry(fulladder_3_carry));
  FullAdder fulladder_4 (.a(a[3]), .b(b[3]), .c(fulladder_3_carry), .sum(out_3[3]), .carry(fulladder_4_carry));
  FullAdder fulladder_5 (.a(a[4]), .b(b[4]), .c(fulladder_4_carry), .sum(out_3[4]), .carry(fulladder_5_carry));
  FullAdder fulladder_6 (.a(a[5]), .b(b[5]), .c(fulladder_5_carry), .sum(out_3[5]), .carry(fulladder_6_carry));
  FullAdder fulladder_7 (.a(a[6]), .b(b[6]), .c(fulladder_6_carry), .sum(out_3[6]), .carry(fulladder_7_carry));
  FullAdder fulladder_8 (.a(a[7]), .b(b[7]), .c(fulladder_7_carry), .sum(out_3[7]), .carry(fulladder_8_carry));
  FullAdder fulladder_9 (.a(a[8]), .b(b[8]), .c(fulladder_8_carry), .sum(out_3[8]), .carry(fulladder_9_carry));
  FullAdder fulladder_10 (.a(a[9]), .b(b[9]), .c(fulladder_9_carry), .sum(out_3[9]), .carry(fulladder_10_carry));
  FullAdder fulladder_11 (.a(a[10]), .b(b[10]), .c(fulladder_10_carry), .sum(out_3[10]), .carry(fulladder_11_carry));
  FullAdder fulladder_12 (.a(a[11]), .b(b[11]), .c(fulladder_11_carry), .sum(out_3[11]), .carry(fulladder_12_carry));
  FullAdder fulladder_13 (.a(a[12]), .b(b[12]), .c(fulladder_12_carry), .sum(out_3[12]), .carry(fulladder_13_carry));
  FullAdder fulladder_14 (.a(a[13]), .b(b[13]), .c(fulladder_13_carry), .sum(out_3[13]), .carry(fulladder_14_carry));
  FullAdder fulladder_15 (.a(a[14]), .b(b[14]), .c(fulladder_14_carry), .sum(out_3[14]), .carry(fulladder_15_carry));
  FullAdder fulladder_16 (.a(a[15]), .b(b[15]), .c(fulladder_15_carry), .sum(out_3[15]));  // open: carry
endmodule

module Inc16 (
  input  [15:0] inp,
  output [15:0] outp
);

  wire and_1_out, and_2_out, and_3_out, and_4_out, and_5_out, and_6_out, and_7_out, and_8_out, and_9_out,
       and_10_out, and_11_out, and_12_out, and_13_out, and_14_out, and_15_out, and_16_out;

  xor xor_1 (outp[0], 1'b1, inp[0]);
  and and_1 (and_1_out, 1'b1, inp[0]);
  xor xor_2 (outp[1], and_1_out, inp[1]);
  and and_2 (and_2_out, and_1_out, inp[1]);
  xor xor_3 (outp[2], and_2_out, inp[2]);
  and and_3 (and_3_out, and_2_out, inp[2]);
  xor xor_4 (outp[3], and_3_out, inp[3]);
  and and_4 (and_4_out, and_3_out, inp[3]);
  xor xor_5 (outp[4], and_4_out, inp[4]);
  and and_5 (and_5_out, and_4_out, inp[4]);
  xor xor_6 (outp[5], and_5_out, inp[5]);
  and and_6 (and_6_out, and_5_out, inp[5]);
  xor xor_7 (outp[6], and_6_out, inp[6]);
  and and_7 (and_7_out, and_6_out, inp[6]);
  xor xor_8 (outp[7], and_7_out, inp[7]);
  and and_8 (and_8_out, and_7_out, inp[7]);
  xor xor_9 (outp[8], and_8_out, inp[8]);
  and and_9 (and_9_out, and_8_out, inp[8]);
  xor xor_10 (outp[9], and_9_out, inp[9]);
  and and_10 (and_10_out, and_9_out, inp[9]);
  xor xor_11 (outp[10], and_10_out, inp[10]);
  and and_11 (and_11_out, and_10_out, inp[10]);
  xor xor_12 (outp[11], and_11_out, inp[11]);
  and and_12 (and_12_out, and_11_out, inp[11]);
  xor xor_13 (outp[12], and_12_out, inp[12]);
  and and_13 (and_13_out, and_12_out, inp[12]);
  xor xor_14 (outp[13], and_13_out, inp[13]);
  and and_14 (and_14_out, and_13_out, inp[13]);
  xor xor_15 (outp[14], and_14_out, inp[14]);
  and and_15 (and_15_out, and_14_out, inp[14]);
  xor xor_16 (outp[15], and_15_out, inp[15]);
  and and_16 (and_16_out, and_15_out, inp[15]);
endmodule

module Inc16C (
  input  [15:0] in_1,
  output [15:0] out_2
);

  wire halfadder_1_carry, halfadder_2_carry, halfadder_3_carry, halfadder_4_carry, halfadder_5_carry,
       halfadder_6_carry, halfadder_7_carry, halfadder_8_carry, halfadder_9_carry, halfadder_10_carry,
       halfadder_11_carry, halfadder_12_carry, halfadder_13_carry, halfadder_14_carry, halfadder_15_carry,
       halfadder_16_carry;

  HalfAdder halfadder_1 (.a(1'b1), .b(in_1[0]), .sum(out_2[0]), .carry(halfadder_1_carry));
  HalfAdder halfadder_2 (.a(halfadder_1_carry), .b(in_1[1]), .sum(out_2[1]), .carry(halfadder_2_carry));
  HalfAdder halfadder_3 (.a(halfadder_2_carry), .b(in_1[2]), .sum(out_2[2]), .carry(halfadder_3_carry));
  HalfAdder halfadder_4 (.a(halfadder_3_carry), .b(in_1[3]), .sum(out_2[3]), .carry(halfadder_4_carry));
  HalfAdder halfadder_5 (.a(halfadder_4_carry), .b(in_1[4]), .sum(out_2[4]), .carry(halfadder_5_carry));
  HalfAdder halfadder_6 (.a(halfadder_5_carry), .b(in_1[5]), .sum(out_2[5]), .carry(halfadder_6_carry));
  HalfAdder halfadder_7 (.a(halfadder_6_carry), .b(in_1[6]), .sum(out_2[6]), .carry(halfadder_7_carry));
  HalfAdder halfadder_8 (.a(halfadder_7_carry), .b(in_1[7]), .sum(out_2[7]), .carry(halfadder_8_carry));
  HalfAdder halfadder_9 (.a(halfadder_8_carry), .b(in_1[8]), .sum(out_2[8]), .carry(halfadder_9_carry));
  HalfAdder halfadder_10 (.a(halfadder_9_carry), .b(in_1[9]), .sum(out_2[9]), .carry(halfadder_10_carry));
  HalfAdder halfadder_11 (.a(halfadder_10_carry), .b(in_1[10]), .sum(out_2[10]), .carry(halfadder_11_carry));
  HalfAdder halfadder_12 (.a(halfadder_11_carry), .b(in_1[11]), .sum(out_2[11]), .carry(halfadder_12_carry));
  HalfAdder halfadder_13 (.a(halfadder_12_carry), .b(in_1[12]), .sum(out_2[12]), .carry(halfadder_13_carry));
  HalfAdder halfadder_14 (.a(halfadder_13_carry), .b(in_1[13]), .sum(out_2[13]), .carry(halfadder_14_carry));
  HalfAdder halfadder_15 (.a(halfadder_14_carry), .b(in_1[14]), .sum(out_2[14]), .carry(halfadder_15_carry));
  HalfAdder halfadder_16 (.a(halfadder_15_carry), .b(in_1[15]), .sum(out_2[15]), .carry(halfadder_16_carry));
endmodule

module ALU (
  input  [5:0] in_1,
  input  [15:0] x,
  input  [15:0] y,
  output [15:0] out_4
);

  wire and_1_out, and_2_out, and_3_out, and_4_out, and_5_out, and_6_out, and_7_out, and_8_out, and_9_out,
       and_10_out, and_11_out, and_12_out, and_13_out, and_14_out, and_15_out, and_16_out, and_17_out,
       and_18_out, and_19_out, and_20_out, and_21_out, and_22_out, and_23_out, and_24_out, and_25_out,
       and_26_out, and_27_out, and_28_out, and_29_out, and_30_out, and_31_out, and_32_out, and_33_out,
       and_34_out, and_35_out, and_36_out, and_37_out, and_38_out, and_39_out, and_40_out, and_41_out,
       and_42_out, and_43_out, and_44_out, and_45_out, and_46_out, and_47_out, and_48_out, and_49_out,
       and_50_out, and_51_out, and_52_out, and_53_out, and_54_out, and_55_out, and_56_out, and_57_out,
       and_58_out, and_59_out, and_60_out, and_61_out, and_62_out, and_63_out, and_64_out, and_65_out,
       and_66_out, and_67_out, and_68_out, and_69_out, and_70_out, and_71_out, and_72_out, and_73_out,
       and_74_out, and_75_out, and_76_out, and_77_out, and_78_out, and_79_out, and_80_out, and_81_out,
       and_82_out, and_83_out, and_84_out, and_85_out, and_86_out, and_87_out, and_88_out, and_89_out,
       and_90_out, and_91_out, and_92_out, and_93_out, and_94_out, and_95_out, and_96_out, and_113_out,
       and_114_out, and_115_out, and_116_out, and_117_out, and_118_out, and_119_out, and_120_out,
       and_121_out, and_122_out, and_123_out, and_124_out, and_125_out, and_126_out, and_127_out,
       and_128_out, and_129_out, and_130_out, and_131_out, and_132_out, and_133_out, and_134_out,
       and_135_out, and_136_out, and_137_out, and_138_out, and_139_out, and_140_out, and_141_out,
       and_142_out, and_143_out, and_144_out, and_145_out, and_146_out, and_147_out, and_148_out,
       and_149_out, and_150_out, and_151_out, and_152_out, and_153_out, and_154_out, and_155_out,
       and_156_out, and_157_out, and_158_out, and_159_out, and_160_out, and_161_out, and_162_out,
       and_163_out, and_164_out, and_165_out, and_166_out, and_167_out, and_168_out, and_169_out,
       and_170_out, and_171_out, and_172_out, and_173_out, and_174_out, and_175_out, and_176_out,
       and_177_out, and_178_out, and_179_out, and_180_out, and_181_out, and_182_out, and_183_out,
       and_184_out, and_185_out, and_186_out, and_187_out, and_188_out, and_189_out, and_190_out,
       and_191_out, and_192_out, and_193_out, and_194_out, and_195_out, and_196_out, and_197_out,
       and_198_out, and_199_out, and_200_out, and_201_out, and_202_out, and_203_out, and_204_out,
       and_205_out, and_206_out, and_207_out, and_208_out, not_1_out, not_2_out, not_3_out, not_4_out,
       not_5_out, not_6_out, not_7_out, not_8_out, not_9_out, not_10_out, not_11_out, not_12_out, not_13_out,
       not_14_out, not_15_out, not_16_out, not_17_out, not_18_out, not_19_out, not_20_out, not_21_out,
       not_22_out, not_23_out, not_24_out, not_25_out, not_26_out, not_27_out, not_28_out, not_29_out,
       not_30_out, not_31_out, not_32_out, not_33_out, not_34_out, not_35_out, not_36_out, not_37_out,
       not_38_out, not_39_out, not_40_out, not_41_out, not_42_out, not_43_out, not_44_out, not_45_out,
       not_46_out, not_47_out, not_48_out, not_49_out, not_50_out, not_51_out, not_52_out, not_53_out,
       not_54_out, not_55_out, not_56_out, not_57_out, not_58_out, not_59_out, not_60_out, not_61_out,
       not_62_out, not_63_out, not_64_out, not_65_out, not_66_out, not_67_out, not_68_out, not_69_out,
       not_70_out, not_71_out, not_72_out, not_73_out, not_74_out, not_75_out, not_76_out, not_77_out,
       not_78_out, not_79_out, not_80_out, not_81_out, not_82_out, not_83_out, not_84_out, not_85_out,
       not_86_out, not_87_out, not_88_out, not_89_out, not_90_out, not_91_out, not_92_out, not_93_out,
       not_94_out, not_95_out, not_96_out, not_97_out, not_98_out, not_99_out, not_100_out, not_101_out,
       not_102_out, not_103_out, not_104_out, not_105_out, not_106_out, not_107_out, not_108_out,
       not_109_out, not_110_out, not_111_out, not_112_out, not_113_out, not_114_out, not_115_out, or_33_out,
       or_34_out, or_35_out, or_36_out, or_37_out, or_38_out, or_39_out, or_40_out, or_41_out, or_42_out,
       or_43_out, or_44_out, or_45_out, or_46_out, or_47_out, or_48_out, or_49_out, or_50_out, or_51_out,
       or_52_out, or_53_out, or_54_out, or_55_out, or_56_out, or_57_out, or_58_out, or_59_out, or_60_out,
       or_61_out, or_62_out, or_63_out, or_64_out, xor_1_out, xor_2_out, xor_3_out, xor_4_out, xor_5_out,
       xor_6_out, xor_7_out, xor_8_out, xor_9_out, xor_10_out, xor_11_out, xor_12_out, xor_13_out,
       xor_14_out, xor_15_out, xor_16_out, xor_17_out, xor_18_out, xor_19_out, xor_20_out, xor_21_out,
       xor_22_out, xor_23_out, xor_24_out, xor_25_out, xor_26_out, xor_27_out, xor_28_out, xor_29_out,
       xor_30_out, xor_31_out, xor_32_out;
  wire [15:0] and_97_out, or_1_out, or_17_out;

  // Probe on x
  // Probe on y
  // Probe on out_4
  // Probe on out_4
  not not_1 (not_1_out, in_1[5]);
  and and_1 (and_1_out, x[0], not_1_out);
  and and_2 (and_2_out, x[1], not_1_out);
  and and_3 (and_3_out, x[2], not_1_out);
  and and_4 (and_4_out, x[3], not_1_out);
  and and_5 (and_5_out, x[4], not_1_out);
  and and_6 (and_6_out, x[5], not_1_out);
  and and_7 (and_7_out, x[6], not_1_out);
  and and_8 (and_8_out, x[7], not_1_out);
  and and_9 (and_9_out, x[8], not_1_out);
  and and_10 (and_10_out, x[9], not_1_out);
  and and_11 (and_11_out, x[10], not_1_out);
  and and_12 (and_12_out, x[11], not_1_out);
  and and_13 (and_13_out, x[12], not_1_out);
  and and_14 (and_14_out, x[13], not_1_out);
  and and_15 (and_15_out, x[14], not_1_out);
  and and_16 (and_16_out, x[15], not_1_out);
  not not_2 (not_2_out, in_1[3]);
  not not_3 (not_3_out, in_1[4]);
  not not_4 (not_4_out, and_1_out);
  not not_5 (not_5_out, in_1[4]);
  not not_6 (not_6_out, and_2_out);
  not not_7 (not_7_out, in_1[4]);
  not not_8 (not_8_out, and_3_out);
  not not_9 (not_9_out, in_1[4]);
  not not_10 (not_10_out, and_4_out);
  not not_11 (not_11_out, in_1[4]);
  not not_12 (not_12_out, and_5_out);
  not not_13 (not_13_out, in_1[4]);
  not not_14 (not_14_out, and_6_out);
  not not_15 (not_15_out, in_1[4]);
  not not_16 (not_16_out, and_7_out);
  not not_17 (not_17_out, in_1[4]);
  not not_18 (not_18_out, and_8_out);
  not not_19 (not_19_out, in_1[4]);
  not not_20 (not_20_out, and_9_out);
  not not_21 (not_21_out, in_1[4]);
  not not_22 (not_22_out, and_10_out);
  not not_23 (not_23_out, in_1[4]);
  not not_24 (not_24_out, and_11_out);
  not not_25 (not_25_out, in_1[4]);
  not not_26 (not_26_out, and_12_out);
  not not_27 (not_27_out, in_1[4]);
  not not_28 (not_28_out, and_13_out);
  not not_29 (not_29_out, in_1[4]);
  not not_30 (not_30_out, and_14_out);
  not not_31 (not_31_out, in_1[4]);
  not not_32 (not_32_out, and_15_out);
  not not_33 (not_33_out, in_1[4]);
  not not_34 (not_34_out, and_16_out);
  and and_17 (and_17_out, and_1_out, not_3_out);
  and and_18 (and_18_out, not_4_out, in_1[4]);
  and and_19 (and_19_out, and_2_out, not_5_out);
  and and_20 (and_20_out, not_6_out, in_1[4]);
  and and_21 (and_21_out, and_3_out, not_7_out);
  and and_22 (and_22_out, not_8_out, in_1[4]);
  and and_23 (and_23_out, and_4_out, not_9_out);
  and and_24 (and_24_out, not_10_out, in_1[4]);
  and and_25 (and_25_out, and_5_out, not_11_out);
  and and_26 (and_26_out, not_12_out, in_1[4]);
  and and_27 (and_27_out, and_6_out, not_13_out);
  and and_28 (and_28_out, not_14_out, in_1[4]);
  and and_29 (and_29_out, and_7_out, not_15_out);
  and and_30 (and_30_out, not_16_out, in_1[4]);
  and and_31 (and_31_out, and_8_out, not_17_out);
  and and_32 (and_32_out, not_18_out, in_1[4]);
  and and_33 (and_33_out, and_9_out, not_19_out);
  and and_34 (and_34_out, not_20_out, in_1[4]);
  and and_35 (and_35_out, and_10_out, not_21_out);
  and and_36 (and_36_out, not_22_out, in_1[4]);
  and and_37 (and_37_out, and_11_out, not_23_out);
  and and_38 (and_38_out, not_24_out, in_1[4]);
  and and_39 (and_39_out, and_12_out, not_25_out);
  and and_40 (and_40_out, not_26_out, in_1[4]);
  and and_41 (and_41_out, and_13_out, not_27_out);
  and and_42 (and_42_out, not_28_out, in_1[4]);
  and and_43 (and_43_out, and_14_out, not_29_out);
  and and_44 (and_44_out, not_30_out, in_1[4]);
  and and_45 (and_45_out, and_15_out, not_31_out);
  and and_46 (and_46_out, not_32_out, in_1[4]);
  and and_47 (and_47_out, and_16_out, not_33_out);
  and and_48 (and_48_out, not_34_out, in_1[4]);
  or or_1 (or_1_out[0], and_17_out, and_18_out);
  or or_2 (or_1_out[1], and_19_out, and_20_out);
  or or_3 (or_1_out[2], and_21_out, and_22_out);
  or or_4 (or_1_out[3], and_23_out, and_24_out);
  or or_5 (or_1_out[4], and_25_out, and_26_out);
  or or_6 (or_1_out[5], and_27_out, and_28_out);
  or or_7 (or_1_out[6], and_29_out, and_30_out);
  or or_8 (or_1_out[7], and_31_out, and_32_out);
  or or_9 (or_1_out[8], and_33_out, and_34_out);
  or or_10 (or_1_out[9], and_35_out, and_36_out);
  or or_11 (or_1_out[10], and_37_out, and_38_out);
  or or_12 (or_1_out[11], and_39_out, and_40_out);
  or or_13 (or_1_out[12], and_41_out, and_42_out);
  or or_14 (or_1_out[13], and_43_out, and_44_out);
  or or_15 (or_1_out[14], and_45_out, and_46_out);
  or or_16 (or_1_out[15], and_47_out, and_48_out);
  and and_49 (and_49_out, y[0], not_2_out);
  and and_50 (and_50_out, y[1], not_2_out);
  and and_51 (and_51_out, y[2], not_2_out);
  and and_52 (and_52_out, y[3], not_2_out);
  and and_53 (and_53_out, y[4], not_2_out);
  and and_54 (and_54_out, y[5], not_2_out);
  and and_55 (and_55_out, y[6], not_2_out);
  and and_56 (and_56_out, y[7], not_2_out);
  and and_57 (and_57_out, y[8], not_2_out);
  and and_58 (and_58_out, y[9], not_2_out);
  and and_59 (and_59_out, y[10], not_2_out);
  and and_60 (and_60_out, y[11], not_2_out);
  and and_61 (and_61_out, y[12], not_2_out);
  and and_62 (and_62_out, y[13], not_2_out);
  and and_63 (and_63_out, y[14], not_2_out);
  and and_64 (and_64_out, y[15], not_2_out);
  not not_35 (not_35_out, in_1[2]);
  not not_36 (not_36_out, and_49_out);
  not not_37 (not_37_out, in_1[2]);
  not not_38 (not_38_out, and_50_out);
  not not_39 (not_39_out, in_1[2]);
  not not_40 (not_40_out, and_51_out);
  not not_41 (not_41_out, in_1[2]);
  not not_42 (not_42_out, and_52_out);
  not not_43 (not_43_out, in_1[2]);
  not not_44 (not_44_out, and_53_out);
  not not_45 (not_45_out, in_1[2]);
  not not_46 (not_46_out, and_54_out);
  not not_47 (not_47_out, in_1[2]);
  not not_48 (not_48_out, and_55_out);
  not not_49 (not_49_out, in_1[2]);
  not not_50 (not_50_out, and_56_out);
  not not_51 (not_51_out, in_1[2]);
  not not_52 (not_52_out, and_57_out);
  not not_53 (not_53_out, in_1[2]);
  not not_54 (not_54_out, and_58_out);
  not not_55 (not_55_out, in_1[2]);
  not not_56 (not_56_out, and_59_out);
  not not_57 (not_57_out, in_1[2]);
  not not_58 (not_58_out, and_60_out);
  not not_59 (not_59_out, in_1[2]);
  not not_60 (not_60_out, and_61_out);
  not not_61 (not_61_out, in_1[2]);
  not not_62 (not_62_out, and_62_out);
  not not_63 (not_63_out, in_1[2]);
  not not_64 (not_64_out, and_63_out);
  not not_65 (not_65_out, in_1[2]);
  not not_66 (not_66_out, and_64_out);
  and and_65 (and_65_out, and_49_out, not_35_out);
  and and_66 (and_66_out, not_36_out, in_1[2]);
  and and_67 (and_67_out, and_50_out, not_37_out);
  and and_68 (and_68_out, not_38_out, in_1[2]);
  and and_69 (and_69_out, and_51_out, not_39_out);
  and and_70 (and_70_out, not_40_out, in_1[2]);
  and and_71 (and_71_out, and_52_out, not_41_out);
  and and_72 (and_72_out, not_42_out, in_1[2]);
  and and_73 (and_73_out, and_53_out, not_43_out);
  and and_74 (and_74_out, not_44_out, in_1[2]);
  and and_75 (and_75_out, and_54_out, not_45_out);
  and and_76 (and_76_out, not_46_out, in_1[2]);
  and and_77 (and_77_out, and_55_out, not_47_out);
  and and_78 (and_78_out, not_48_out, in_1[2]);
  and and_79 (and_79_out, and_56_out, not_49_out);
  and and_80 (and_80_out, not_50_out, in_1[2]);
  and and_81 (and_81_out, and_57_out, not_51_out);
  and and_82 (and_82_out, not_52_out, in_1[2]);
  and and_83 (and_83_out, and_58_out, not_53_out);
  and and_84 (and_84_out, not_54_out, in_1[2]);
  and and_85 (and_85_out, and_59_out, not_55_out);
  and and_86 (and_86_out, not_56_out, in_1[2]);
  and and_87 (and_87_out, and_60_out, not_57_out);
  and and_88 (and_88_out, not_58_out, in_1[2]);
  and and_89 (and_89_out, and_61_out, not_59_out);
  and and_90 (and_90_out, not_60_out, in_1[2]);
  and and_91 (and_91_out, and_62_out, not_61_out);
  and and_92 (and_92_out, not_62_out, in_1[2]);
  and and_93 (and_93_out, and_63_out, not_63_out);
  and and_94 (and_94_out, not_64_out, in_1[2]);
  and and_95 (and_95_out, and_64_out, not_65_out);
  and and_96 (and_96_out, not_66_out, in_1[2]);
  or or_17 (or_17_out[0], and_65_out, and_66_out);
  or or_18 (or_17_out[1], and_67_out, and_68_out);
  or or_19 (or_17_out[2], and_69_out, and_70_out);
  or or_20 (or_17_out[3], and_71_out, and_72_out);
  or or_21 (or_17_out[4], and_73_out, and_74_out);
  or or_22 (or_17_out[5], and_75_out, and_76_out);
  or or_23 (or_17_out[6], and_77_out, and_78_out);
  or or_24 (or_17_out[7], and_79_out, and_80_out);
  or or_25 (or_17_out[8], and_81_out, and_82_out);
  or or_26 (or_17_out[9], and_83_out, and_84_out);
  or or_27 (or_17_out[10], and_85_out, and_86_out);
  or or_28 (or_17_out[11], and_87_out, and_88_out);
  or or_29 (or_17_out[12], and_89_out, and_90_out);
  or or_30 (or_17_out[13], and_91_out, and_92_out);
  or or_31 (or_17_out[14], and_93_out, and_94_out);
  or or_32 (or_17_out[15], and_95_out, and_96_out);
  and and_97 (and_97_out[0], or_1_out[0], or_17_out[0]);
  and and_98 (and_97_out[1], or_1_out[1], or_17_out[1]);
  and and_99 (and_97_out[2], or_1_out[2], or_17_out[2]);
  and and_100 (and_97_out[3], or_1_out[3], or_17_out[3]);
  and and_101 (and_97_out[4], or_1_out[4], or_17_out[4]);
  and and_102 (and_97_out[5], or_1_out[5], or_17_out[5]);
  and and_103 (and_97_out[6], or_1_out[6], or_17_out[6]);
  and and_104 (and_97_out[7], or_1_out[7], or_17_out[7]);
  and and_105 (and_97_out[8], or_1_out[8], or_17_out[8]);
  and and_106 (and_97_out[9], or_1_out[9], or_17_out[9]);
  and and_107 (and_97_out[10], or_1_out[10], or_17_out[10]);
  and and_108 (and_97_out[11], or_1_out[11], or_17_out[11]);
  and and_109 (and_97_out[12], or_1_out[12], or_17_out[12]);
  and and_110 (and_97_out[13], or_1_out[13], or_17_out[13]);
  and and_111 (and_97_out[14], or_1_out[14], or_17_out[14]);
  and and_112 (and_97_out[15], or_1_out[15], or_17_out[15]);
  xor xor_1 (xor_1_out, or_1_out[0], or_17_out[0]);
  xor xor_2 (xor_2_out, or_1_out[1], or_17_out[1]);
  xor xor_3 (xor_3_out, or_1_out[2], or_17_out[2]);
  xor xor_4 (xor_4_out, or_1_out[3], or_17_out[3]);
  xor xor_5 (xor_5_out, or_1_out[4], or_17_out[4]);
  xor xor_6 (xor_6_out, or_1_out[5], or_17_out[5]);
  xor xor_7 (xor_7_out, or_1_out[6], or_17_out[6]);
  xor xor_8 (xor_8_out, or_1_out[7], or_17_out[7]);
  xor xor_9 (xor_9_out, or_1_out[8], or_17_out[8]);
  xor xor_10 (xor_10_out, or_1_out[9], or_17_out[9]);
  xor xor_11 (xor_11_out, or_1_out[10], or_17_out[10]);
  xor xor_12 (xor_12_out, or_1_out[11], or_17_out[11]);
  xor xor_13 (xor_13_out, or_1_out[12], or_17_out[12]);
  xor xor_14 (xor_14_out, or_1_out[13], or_17_out[13]);
  xor xor_15 (xor_15_out, or_1_out[14], or_17_out[14]);
  xor xor_16 (xor_16_out, or_1_out[15], or_17_out[15]);
  xor xor_17 (xor_17_out, xor_1_out, 1'b0);
  and and_113 (and_113_out, xor_1_out, 1'b0);
  and and_114 (and_114_out, or_1_out[0], or_17_out[0]);
  xor xor_18 (xor_18_out, xor_2_out, or_33_out);
  and and_115 (and_115_out, xor_2_out, or_33_out);
  and and_116 (and_116_out, or_1_out[1], or_17_out[1]);
  xor xor_19 (xor_19_out, xor_3_out, or_34_out);
  and and_117 (and_117_out, xor_3_out, or_34_out);
  and and_118 (and_118_out, or_1_out[2], or_17_out[2]);
  xor xor_20 (xor_20_out, xor_4_out, or_35_out);
  and and_119 (and_119_out, xor_4_out, or_35_out);
  and and_120 (and_120_out, or_1_out[3], or_17_out[3]);
  xor xor_21 (xor_21_out, xor_5_out, or_36_out);
  and and_121 (and_121_out, xor_5_out, or_36_out);
  and and_122 (and_122_out, or_1_out[4], or_17_out[4]);
  xor xor_22 (xor_22_out, xor_6_out, or_37_out);
  and and_123 (and_123_out, xor_6_out, or_37_out);
  and and_124 (and_124_out, or_1_out[5], or_17_out[5]);
  xor xor_23 (xor_23_out, xor_7_out, or_38_out);
  and and_125 (and_125_out, xor_7_out, or_38_out);
  and and_126 (and_126_out, or_1_out[6], or_17_out[6]);
  xor xor_24 (xor_24_out, xor_8_out, or_39_out);
  and and_127 (and_127_out, xor_8_out, or_39_out);
  and and_128 (and_128_out, or_1_out[7], or_17_out[7]);
  xor xor_25 (xor_25_out, xor_9_out, or_40_out);
  and and_129 (and_129_out, xor_9_out, or_40_out);
  and and_130 (and_130_out, or_1_out[8], or_17_out[8]);
  xor xor_26 (xor_26_out, xor_10_out, or_41_out);
  and and_131 (and_131_out, xor_10_out, or_41_out);
  and and_132 (and_132_out, or_1_out[9], or_17_out[9]);
  xor xor_27 (xor_27_out, xor_11_out, or_42_out);
  and and_133 (and_133_out, xor_11_out, or_42_out);
  and and_134 (and_134_out, or_1_out[10], or_17_out[10]);
  xor xor_28 (xor_28_out, xor_12_out, or_43_out);
  and and_135 (and_135_out, xor_12_out, or_43_out);
  and and_136 (and_136_out, or_1_out[11], or_17_out[11]);
  xor xor_29 (xor_29_out, xor_13_out, or_44_out);
  and and_137 (and_137_out, xor_13_out, or_44_out);
  and and_138 (and_138_out, or_1_out[12], or_17_out[12]);
  xor xor_30 (xor_30_out, xor_14_out, or_45_out);
  and and_139 (and_139_out, xor_14_out, or_45_out);
  and and_140 (and_140_out, or_1_out[13], or_17_out[13]);
  xor xor_31 (xor_31_out, xor_15_out, or_46_out);
  and and_141 (and_141_out, xor_15_out, or_46_out);
  and and_142 (and_142_out, or_1_out[14], or_17_out[14]);
  xor xor_32 (xor_32_out, xor_16_out, or_47_out);
  and and_143 (and_143_out, xor_16_out, or_47_out);
  and and_144 (and_144_out, or_1_out[15], or_17_out[15]);
  or or_33 (or_33_out, and_113_out, and_114_out);
  or or_34 (or_34_out, and_115_out, and_116_out);
  or or_35 (or_35_out, and_117_out, and_118_out);
  or or_36 (or_36_out, and_119_out, and_120_out);
  or or_37 (or_37_out, and_121_out, and_122_out);
  or or_38 (or_38_out, and_123_out, and_124_out);
  or or_39 (or_39_out, and_125_out, and_126_out);
  or or_40 (or_40_out, and_127_out, and_128_out);
  or or_41 (or_41_out, and_129_out, and_130_out);
  or or_42 (or_42_out, and_131_out, and_132_out);
  or or_43 (or_43_out, and_133_out, and_134_out);
  or or_44 (or_44_out, and_135_out, and_136_out);
  or or_45 (or_45_out, and_137_out, and_138_out);
  or or_46 (or_46_out, and_139_out, and_140_out);
  or or_47 (or_47_out, and_141_out, and_142_out);
  or or_48 (or_48_out, and_143_out, and_144_out);
  not not_67 (not_67_out, in_1[1]);
  not not_68 (not_68_out, not_67_out);
  not not_69 (not_69_out, not_67_out);
  not not_70 (not_70_out, not_67_out);
  not not_71 (not_71_out, not_67_out);
  not not_72 (not_72_out, not_67_out);
  not not_73 (not_73_out, not_67_out);
  not not_74 (not_74_out, not_67_out);
  not not_75 (not_75_out, not_67_out);
  not not_76 (not_76_out, not_67_out);
  not not_77 (not_77_out, not_67_out);
  not not_78 (not_78_out, not_67_out);
  not not_79 (not_79_out, not_67_out);
  not not_80 (not_80_out, not_67_out);
  not not_81 (not_81_out, not_67_out);
  not not_82 (not_82_out, not_67_out);
  not not_83 (not_83_out, not_67_out);
  and and_145 (and_145_out, xor_17_out, not_68_out);
  and and_146 (and_146_out, and_97_out[0], not_67_out);
  and and_147 (and_147_out, xor_18_out, not_69_out);
  and and_148 (and_148_out, and_97_out[1], not_67_out);
  and and_149 (and_149_out, xor_19_out, not_70_out);
  and and_150 (and_150_out, and_97_out[2], not_67_out);
  and and_151 (and_151_out, xor_20_out, not_71_out);
  and and_152 (and_152_out, and_97_out[3], not_67_out);
  and and_153 (and_153_out, xor_21_out, not_72_out);
  and and_154 (and_154_out, and_97_out[4], not_67_out);
  and and_155 (and_155_out, xor_22_out, not_73_out);
  and and_156 (and_156_out, and_97_out[5], not_67_out);
  and and_157 (and_157_out, xor_23_out, not_74_out);
  and and_158 (and_158_out, and_97_out[6], not_67_out);
  and and_159 (and_159_out, xor_24_out, not_75_out);
  and and_160 (and_160_out, and_97_out[7], not_67_out);
  and and_161 (and_161_out, xor_25_out, not_76_out);
  and and_162 (and_162_out, and_97_out[8], not_67_out);
  and and_163 (and_163_out, xor_26_out, not_77_out);
  and and_164 (and_164_out, and_97_out[9], not_67_out);
  and and_165 (and_165_out, xor_27_out, not_78_out);
  and and_166 (and_166_out, and_97_out[10], not_67_out);
  and and_167 (and_167_out, xor_28_out, not_79_out);
  and and_168 (and_168_out, and_97_out[11], not_67_out);
  and and_169 (and_169_out, xor_29_out, not_80_out);
  and and_170 (and_170_out, and_97_out[12], not_67_out);
  and and_171 (and_171_out, xor_30_out, not_81_out);
  and and_172 (and_172_out, and_97_out[13], not_67_out);
  and and_173 (and_173_out, xor_31_out, not_82_out);
  and and_174 (and_174_out, and_97_out[14], not_67_out);
  and and_175 (and_175_out, xor_32_out, not_83_out);
  and and_176 (and_176_out, and_97_out[15], not_67_out);
  or or_49 (or_49_out, and_145_out, and_146_out);
  or or_50 (or_50_out, and_147_out, and_148_out);
  or or_51 (or_51_out, and_149_out, and_150_out);
  or or_52 (or_52_out, and_151_out, and_152_out);
  or or_53 (or_53_out, and_153_out, and_154_out);
  or or_54 (or_54_out, and_155_out, and_156_out);
  or or_55 (or_55_out, and_157_out, and_158_out);
  or or_56 (or_56_out, and_159_out, and_160_out);
  or or_57 (or_57_out, and_161_out, and_162_out);
  or or_58 (or_58_out, and_163_out, and_164_out);
  or or_59 (or_59_out, and_165_out, and_166_out);
  or or_60 (or_60_out, and_167_out, and_168_out);
  or or_61 (or_61_out, and_169_out, and_170_out);
  or or_62 (or_62_out, and_171_out, and_172_out);
  or or_63 (or_63_out, and_173_out, and_174_out);
  or or_64 (or_64_out, and_175_out, and_176_out);
  not not_84 (not_84_out, or_49_out);
  not not_85 (not_85_out, or_50_out);
  not not_86 (not_86_out, or_51_out);
  not not_87 (not_87_out, or_52_out);
  not not_88 (not_88_out, or_53_out);
  not not_89 (not_89_out, or_54_out);
  not not_90 (not_90_out, or_55_out);
  not not_91 (not_91_out, or_56_out);
  not not_92 (not_92_out, or_57_out);
  not not_93 (not_93_out, or_58_out);
  not not_94 (not_94_out, or_59_out);
  not not_95 (not_95_out, or_60_out);
  not not_96 (not_96_out, or_61_out);
  not not_97 (not_97_out, or_62_out);
  not not_98 (not_98_out, or_63_out);
  not not_99 (not_99_out, or_64_out);
  not not_100 (not_100_out, in_1[0]);
  not not_101 (not_101_out, in_1[0]);
  not not_102 (not_102_out, in_1[0]);
  not not_103 (not_103_out, in_1[0]);
  not not_104 (not_104_out, in_1[0]);
  not not_105 (not_105_out, in_1[0]);
  not not_106 (not_106_out, in_1[0]);
  not not_107 (not_107_out, in_1[0]);
  not not_108 (not_108_out, in_1[0]);
  not not_109 (not_109_out, in_1[0]);
  not not_110 (not_110_out, in_1[0]);
  not not_111 (not_111_out, in_1[0]);
  not not_112 (not_112_out, in_1[0]);
  not not_113 (not_113_out, in_1[0]);
  not not_114 (not_114_out, in_1[0]);
  not not_115 (not_115_out, in_1[0]);
  and and_177 (and_177_out, or_49_out, not_100_out);
  and and_178 (and_178_out, not_84_out, in_1[0]);
  and and_179 (and_179_out, or_50_out, not_101_out);
  and and_180 (and_180_out, not_85_out, in_1[0]);
  and and_181 (and_181_out, or_51_out, not_102_out);
  and and_182 (and_182_out, not_86_out, in_1[0]);
  and and_183 (and_183_out, or_52_out, not_103_out);
  and and_184 (and_184_out, not_87_out, in_1[0]);
  and and_185 (and_185_out, or_53_out, not_104_out);
  and and_186 (and_186_out, not_88_out, in_1[0]);
  and and_187 (and_187_out, or_54_out, not_105_out);
  and and_188 (and_188_out, not_89_out, in_1[0]);
  and and_189 (and_189_out, or_55_out, not_106_out);
  and and_190 (and_190_out, not_90_out, in_1[0]);
  and and_191 (and_191_out, or_56_out, not_107_out);
  and and_192 (and_192_out, not_91_out, in_1[0]);
  and and_193 (and_193_out, or_57_out, not_108_out);
  and and_194 (and_194_out, not_92_out, in_1[0]);
  and and_195 (and_195_out, or_58_out, not_109_out);
  and and_196 (and_196_out, not_93_out, in_1[0]);
  and and_197 (and_197_out, or_59_out, not_110_out);
  and and_198 (and_198_out, not_94_out, in_1[0]);
  and and_199 (and_199_out, or_60_out, not_111_out);
  and and_200 (and_200_out, not_95_out, in_1[0]);
  and and_201 (and_201_out, or_61_out, not_112_out);
  and and_202 (and_202_out, not_96_out, in_1[0]);
  and and_203 (and_203_out, or_62_out, not_113_out);
  and and_204 (and_204_out, not_97_out, in_1[0]);
  and and_205 (and_205_out, or_63_out, not_114_out);
  and and_206 (and_206_out, not_98_out, in_1[0]);
  and and_207 (and_207_out, or_64_out, not_115_out);
  and and_208 (and_208_out, not_99_out, in_1[0]);
  or or_65 (out_4[0], and_177_out, and_178_out);
  or or_66 (out_4[1], and_179_out, and_180_out);
  or or_67 (out_4[2], and_181_out, and_182_out);
  or or_68 (out_4[3], and_183_out, and_184_out);
  or or_69 (out_4[4], and_185_out, and_186_out);
  or or_70 (out_4[5], and_187_out, and_188_out);
  or or_71 (out_4[6], and_189_out, and_190_out);
  or or_72 (out_4[7], and_191_out, and_192_out);
  or or_73 (out_4[8], and_193_out, and_194_out);
  or or_74 (out_4[9], and_195_out, and_196_out);
  or or_75 (out_4[10], and_197_out, and_198_out);
  or or_76 (out_4[11], and_199_out, and_200_out);
  or or_77 (out_4[12], and_201_out, and_202_out);
  or or_78 (out_4[13], and_203_out, and_204_out);
  or or_79 (out_4[14], and_205_out, and_206_out);
  or or_80 (out_4[15], and_207_out, and_208_out);
  // Probe on out_4

  // Other names for the same wires on the sheet: result[15:0] = out_4
endmodule

module ALU_C (
  input  [5:0] control,
  input  [15:0] x,
  input  [15:0] y,
  output [15:0] outp
);

  wire not_1_out, not_2_out;
  wire [15:0] add16_1_sum, and_1_out, and_2_out, and_3_out, bit_extender_1_out, bit_extender_2_out,
       multiplexer_1_out, multiplexer_2_out, multiplexer_3_out, not_3_out, not_4_out, not_5_out;

  // Probe on x
  // Probe on y
  not not_1 (not_1_out, control[5]);
  assign bit_extender_1_out = {{15{not_1_out}}, not_1_out};  // Bit_Extender bit_extender_1
  assign and_1_out = bit_extender_1_out & x;  // AND_Gate and_1, 16 bits wide
  assign and_2_out = bit_extender_2_out & y;  // AND_Gate and_2, 16 bits wide
  not not_2 (not_2_out, control[3]);
  Multiplexer #(.width(16)) multiplexer_1 (.in0(and_1_out), .in1(not_3_out), .out(multiplexer_1_out), .sel(control[4]));
  assign not_3_out = ~and_1_out;  // NOT_Gate not_3, 16 bits wide
  Multiplexer #(.width(16)) multiplexer_2 (.in0(and_2_out), .in1(not_4_out), .out(multiplexer_2_out), .sel(control[2]));
  assign not_4_out = ~and_2_out;  // NOT_Gate not_4, 16 bits wide
  assign bit_extender_2_out = {{15{not_2_out}}, not_2_out};  // Bit_Extender bit_extender_2
  assign and_3_out = multiplexer_1_out & multiplexer_2_out;  // AND_Gate and_3, 16 bits wide
  Add16 add16_1 (.c(1'b0), .a(multiplexer_1_out), .b(multiplexer_2_out), .sum(add16_1_sum));
  Multiplexer #(.width(16)) multiplexer_3 (
    .in0(and_3_out), .in1(add16_1_sum), .out(multiplexer_3_out), .sel(control[1]));
  Multiplexer #(.width(16)) multiplexer_4 (.in0(multiplexer_3_out), .in1(not_5_out), .out(outp), .sel(control[0]));
  assign not_5_out = ~multiplexer_3_out;  // NOT_Gate not_5, 16 bits wide
  // Probe on outp
endmodule

module ALU_TTL (
  input  [5:0] in_1,
  input  [15:0] x,
  input  [15:0] y,
  output [15:0] out_4
);

  wire and_1_out, and_2_out, and_3_out, and_4_out, and_5_out, and_6_out, and_7_out, and_8_out, and_9_out,
       and_10_out, and_11_out, and_12_out, and_13_out, and_14_out, and_15_out, and_16_out, and_17_out,
       and_18_out, and_19_out, and_20_out, and_21_out, and_22_out, and_23_out, and_24_out, and_25_out,
       and_26_out, and_27_out, and_28_out, and_29_out, and_30_out, and_31_out, and_32_out, and_33_out,
       and_34_out, and_35_out, and_36_out, and_37_out, and_38_out, and_39_out, and_40_out, and_41_out,
       and_42_out, and_43_out, and_44_out, and_45_out, and_46_out, and_47_out, and_48_out, and_65_out,
       and_66_out, and_67_out, and_68_out, and_69_out, and_70_out, and_71_out, and_72_out, and_73_out,
       and_74_out, and_75_out, and_76_out, and_77_out, and_78_out, and_79_out, and_80_out, and_81_out,
       and_82_out, and_83_out, and_84_out, and_85_out, and_86_out, and_87_out, and_88_out, and_89_out,
       and_90_out, and_91_out, and_92_out, and_93_out, and_94_out, and_95_out, and_96_out, and_97_out,
       and_98_out, and_99_out, and_100_out, and_101_out, and_102_out, and_103_out, and_104_out, and_105_out,
       and_106_out, and_107_out, and_108_out, and_109_out, and_110_out, and_111_out, and_112_out,
       and_113_out, and_114_out, and_115_out, and_116_out, and_117_out, and_118_out, and_119_out,
       and_120_out, and_121_out, and_122_out, and_123_out, and_124_out, and_125_out, and_126_out,
       and_127_out, and_128_out, and_129_out, and_130_out, and_131_out, and_132_out, and_133_out,
       and_134_out, and_135_out, and_136_out, and_137_out, and_138_out, and_139_out, and_140_out,
       and_141_out, and_142_out, and_143_out, and_144_out, and_145_out, and_146_out, and_147_out,
       and_148_out, and_149_out, and_150_out, and_151_out, and_152_out, and_153_out, and_154_out,
       and_155_out, and_156_out, and_157_out, and_158_out, and_159_out, and_160_out, n7404_1_pin2,
       n7404_1_pin4, n7404_1_pin10, n7404_1_pin12, n7408_1_pin3, n7408_1_pin6, n7408_1_pin8, n7408_1_pin11,
       not_1_out, not_2_out, not_3_out, not_4_out, not_5_out, not_6_out, not_7_out, not_8_out, not_9_out,
       not_10_out, not_11_out, not_12_out, not_13_out, not_14_out, not_15_out, not_16_out, not_17_out,
       not_18_out, not_19_out, not_20_out, not_21_out, not_22_out, not_23_out, not_24_out, not_25_out,
       not_26_out, not_27_out, not_28_out, not_29_out, not_30_out, not_31_out, not_32_out, not_33_out,
       not_34_out, not_35_out, not_36_out, not_37_out, not_38_out, not_39_out, not_40_out, not_41_out,
       not_42_out, not_43_out, not_44_out, not_45_out, not_46_out, not_47_out, not_48_out, not_49_out,
       not_50_out, not_51_out, not_52_out, not_53_out, not_54_out, not_55_out, not_56_out, not_57_out,
       not_58_out, not_59_out, not_60_out, not_61_out, not_62_out, not_63_out, not_64_out, not_65_out,
       not_66_out, not_67_out, not_68_out, not_69_out, not_70_out, not_71_out, not_72_out, not_73_out,
       not_74_out, not_75_out, not_76_out, not_77_out, not_78_out, not_79_out, not_80_out, not_81_out,
       not_82_out, not_83_out, or_17_out, or_18_out, or_19_out, or_20_out, or_21_out, or_22_out, or_23_out,
       or_24_out, or_25_out, or_26_out, or_27_out, or_28_out, or_29_out, or_30_out, or_31_out, or_32_out,
       or_33_out, or_34_out, or_35_out, or_36_out, or_37_out, or_38_out, or_39_out, or_40_out, or_41_out,
       or_42_out, or_43_out, or_44_out, or_45_out, or_46_out, or_47_out, or_48_out, xor_1_out, xor_2_out,
       xor_3_out, xor_4_out, xor_5_out, xor_6_out, xor_7_out, xor_8_out, xor_9_out, xor_10_out, xor_11_out,
       xor_12_out, xor_13_out, xor_14_out, xor_15_out, xor_16_out, xor_17_out, xor_18_out, xor_19_out,
       xor_20_out, xor_21_out, xor_22_out, xor_23_out, xor_24_out, xor_25_out, xor_26_out, xor_27_out,
       xor_28_out, xor_29_out, xor_30_out, xor_31_out, xor_32_out;
  wire [15:0] and_49_out, or_1_out, undriven;

  _7451 #(.ShowInternalStructure("true")) u_7451_1 ();  // open: pin1, pin2, pin3, pin4, pin5, pin6, pin13, pin12, pin11, pin10, pin9, pin8
  _7454 #(.ShowInternalStructure("true")) u_7454_1 ();  // open: pin1, pin2, pin3, pin4, pin5, pin6, pin13, pin12, pin11, pin10, pin9, pin8
  // Probe on x
  // Probe on y
  // Probe on out_4
  // Probe on out_4
  _7458 #(.ShowInternalStructure("true")) u_7458_1 ();  // open: pin1, pin2, pin3, pin4, pin5, pin6, pin13, pin12, pin11, pin10, pin9, pin8
  not not_1 (not_1_out, in_1[5]);
  _7408 #(.ShowInternalStructure("true")) u_7408_1 (
    .pin1(x[2]), .pin2(not_1_out), .pin3(n7408_1_pin3), .pin4(x[3]), .pin5(not_1_out), .pin6(n7408_1_pin6),
    .pin13(x[1]), .pin12(not_1_out), .pin11(n7408_1_pin11), .pin10(x[0]), .pin9(not_1_out),
    .pin8(n7408_1_pin8));
  _7408 #(.ShowInternalStructure("true")) u_7408_2 (
    .pin1(x[6]), .pin2(not_1_out), .pin4(x[7]), .pin5(not_1_out), .pin13(x[5]), .pin12(not_1_out),
    .pin10(x[4]), .pin9(not_1_out));  // open: pin3, pin6, pin11, pin8
  _7408 #(.ShowInternalStructure("true")) u_7408_3 (
    .pin1(x[10]), .pin2(not_1_out), .pin4(x[11]), .pin5(not_1_out), .pin13(x[9]), .pin12(not_1_out),
    .pin10(x[8]), .pin9(not_1_out));  // open: pin3, pin6, pin11, pin8
  _7408 #(.ShowInternalStructure("true")) u_7408_4 (
    .pin1(x[14]), .pin2(not_1_out), .pin4(x[15]), .pin5(not_1_out), .pin13(x[13]), .pin12(not_1_out),
    .pin10(x[12]), .pin9(not_1_out));  // open: pin3, pin6, pin11, pin8
  _7404 #(.ShowInternalStructure("true")) u_7404_1 (
    .pin1(n7408_1_pin6), .pin2(n7404_1_pin2), .pin3(n7408_1_pin3), .pin4(n7404_1_pin4), .pin13(n7408_1_pin8),
    .pin12(n7404_1_pin12), .pin11(n7408_1_pin11), .pin10(n7404_1_pin10));  // open: pin5, pin6, pin9, pin8
  _7404 #(.ShowInternalStructure("true")) u_7404_2 ();  // open: pin1, pin2, pin3, pin4, pin5, pin6, pin13, pin12, pin11, pin10, pin9, pin8
  _7404 #(.ShowInternalStructure("true")) u_7404_3 ();  // open: pin1, pin2, pin3, pin4, pin5, pin6, pin13, pin12, pin11, pin10, pin9, pin8
  _7404 #(.ShowInternalStructure("true")) u_7404_4 ();  // open: pin1, pin2, pin3, pin4, pin5, pin6, pin13, pin12, pin11, pin10, pin9, pin8
  not not_2 (not_2_out, in_1[3]);
  and and_1 (and_1_out, y[0], not_2_out);
  and and_2 (and_2_out, y[1], not_2_out);
  and and_3 (and_3_out, y[2], not_2_out);
  and and_4 (and_4_out, y[3], not_2_out);
  and and_5 (and_5_out, y[4], not_2_out);
  and and_6 (and_6_out, y[5], not_2_out);
  and and_7 (and_7_out, y[6], not_2_out);
  and and_8 (and_8_out, y[7], not_2_out);
  and and_9 (and_9_out, y[8], not_2_out);
  and and_10 (and_10_out, y[9], not_2_out);
  and and_11 (and_11_out, y[10], not_2_out);
  and and_12 (and_12_out, y[11], not_2_out);
  and and_13 (and_13_out, y[12], not_2_out);
  and and_14 (and_14_out, y[13], not_2_out);
  and and_15 (and_15_out, y[14], not_2_out);
  and and_16 (and_16_out, y[15], not_2_out);
  not not_3 (not_3_out, in_1[2]);
  not not_4 (not_4_out, and_1_out);
  not not_5 (not_5_out, in_1[2]);
  not not_6 (not_6_out, and_2_out);
  not not_7 (not_7_out, in_1[2]);
  not not_8 (not_8_out, and_3_out);
  not not_9 (not_9_out, in_1[2]);
  not not_10 (not_10_out, and_4_out);
  not not_11 (not_11_out, in_1[2]);
  not not_12 (not_12_out, and_5_out);
  not not_13 (not_13_out, in_1[2]);
  not not_14 (not_14_out, and_6_out);
  not not_15 (not_15_out, in_1[2]);
  not not_16 (not_16_out, and_7_out);
  not not_17 (not_17_out, in_1[2]);
  not not_18 (not_18_out, and_8_out);
  not not_19 (not_19_out, in_1[2]);
  not not_20 (not_20_out, and_9_out);
  not not_21 (not_21_out, in_1[2]);
  not not_22 (not_22_out, and_10_out);
  not not_23 (not_23_out, in_1[2]);
  not not_24 (not_24_out, and_11_out);
  not not_25 (not_25_out, in_1[2]);
  not not_26 (not_26_out, and_12_out);
  not not_27 (not_27_out, in_1[2]);
  not not_28 (not_28_out, and_13_out);
  not not_29 (not_29_out, in_1[2]);
  not not_30 (not_30_out, and_14_out);
  not not_31 (not_31_out, in_1[2]);
  not not_32 (not_32_out, and_15_out);
  not not_33 (not_33_out, in_1[2]);
  not not_34 (not_34_out, and_16_out);
  and and_17 (and_17_out, and_1_out, not_3_out);
  and and_18 (and_18_out, not_4_out, in_1[2]);
  and and_19 (and_19_out, and_2_out, not_5_out);
  and and_20 (and_20_out, not_6_out, in_1[2]);
  and and_21 (and_21_out, and_3_out, not_7_out);
  and and_22 (and_22_out, not_8_out, in_1[2]);
  and and_23 (and_23_out, and_4_out, not_9_out);
  and and_24 (and_24_out, not_10_out, in_1[2]);
  and and_25 (and_25_out, and_5_out, not_11_out);
  and and_26 (and_26_out, not_12_out, in_1[2]);
  and and_27 (and_27_out, and_6_out, not_13_out);
  and and_28 (and_28_out, not_14_out, in_1[2]);
  and and_29 (and_29_out, and_7_out, not_15_out);
  and and_30 (and_30_out, not_16_out, in_1[2]);
  and and_31 (and_31_out, and_8_out, not_17_out);
  and and_32 (and_32_out, not_18_out, in_1[2]);
  and and_33 (and_33_out, and_9_out, not_19_out);
  and and_34 (and_34_out, not_20_out, in_1[2]);
  and and_35 (and_35_out, and_10_out, not_21_out);
  and and_36 (and_36_out, not_22_out, in_1[2]);
  and and_37 (and_37_out, and_11_out, not_23_out);
  and and_38 (and_38_out, not_24_out, in_1[2]);
  and and_39 (and_39_out, and_12_out, not_25_out);
  and and_40 (and_40_out, not_26_out, in_1[2]);
  and and_41 (and_41_out, and_13_out, not_27_out);
  and and_42 (and_42_out, not_28_out, in_1[2]);
  and and_43 (and_43_out, and_14_out, not_29_out);
  and and_44 (and_44_out, not_30_out, in_1[2]);
  and and_45 (and_45_out, and_15_out, not_31_out);
  and and_46 (and_46_out, not_32_out, in_1[2]);
  and and_47 (and_47_out, and_16_out, not_33_out);
  and and_48 (and_48_out, not_34_out, in_1[2]);
  or or_1 (or_1_out[0], and_17_out, and_18_out);
  or or_2 (or_1_out[1], and_19_out, and_20_out);
  or or_3 (or_1_out[2], and_21_out, and_22_out);
  or or_4 (or_1_out[3], and_23_out, and_24_out);
  or or_5 (or_1_out[4], and_25_out, and_26_out);
  or or_6 (or_1_out[5], and_27_out, and_28_out);
  or or_7 (or_1_out[6], and_29_out, and_30_out);
  or or_8 (or_1_out[7], and_31_out, and_32_out);
  or or_9 (or_1_out[8], and_33_out, and_34_out);
  or or_10 (or_1_out[9], and_35_out, and_36_out);
  or or_11 (or_1_out[10], and_37_out, and_38_out);
  or or_12 (or_1_out[11], and_39_out, and_40_out);
  or or_13 (or_1_out[12], and_41_out, and_42_out);
  or or_14 (or_1_out[13], and_43_out, and_44_out);
  or or_15 (or_1_out[14], and_45_out, and_46_out);
  or or_16 (or_1_out[15], and_47_out, and_48_out);
  and and_49 (and_49_out[0], undriven[0], or_1_out[0]);
  and and_50 (and_49_out[1], undriven[1], or_1_out[1]);
  and and_51 (and_49_out[2], undriven[2], or_1_out[2]);
  and and_52 (and_49_out[3], undriven[3], or_1_out[3]);
  and and_53 (and_49_out[4], undriven[4], or_1_out[4]);
  and and_54 (and_49_out[5], undriven[5], or_1_out[5]);
  and and_55 (and_49_out[6], undriven[6], or_1_out[6]);
  and and_56 (and_49_out[7], undriven[7], or_1_out[7]);
  and and_57 (and_49_out[8], undriven[8], or_1_out[8]);
  and and_58 (and_49_out[9], undriven[9], or_1_out[9]);
  and and_59 (and_49_out[10], undriven[10], or_1_out[10]);
  and and_60 (and_49_out[11], undriven[11], or_1_out[11]);
  and and_61 (and_49_out[12], undriven[12], or_1_out[12]);
  and and_62 (and_49_out[13], undriven[13], or_1_out[13]);
  and and_63 (and_49_out[14], undriven[14], or_1_out[14]);
  and and_64 (and_49_out[15], undriven[15], or_1_out[15]);
  xor xor_1 (xor_1_out, undriven[0], or_1_out[0]);
  xor xor_2 (xor_2_out, undriven[1], or_1_out[1]);
  xor xor_3 (xor_3_out, undriven[2], or_1_out[2]);
  xor xor_4 (xor_4_out, undriven[3], or_1_out[3]);
  xor xor_5 (xor_5_out, undriven[4], or_1_out[4]);
  xor xor_6 (xor_6_out, undriven[5], or_1_out[5]);
  xor xor_7 (xor_7_out, undriven[6], or_1_out[6]);
  xor xor_8 (xor_8_out, undriven[7], or_1_out[7]);
  xor xor_9 (xor_9_out, undriven[8], or_1_out[8]);
  xor xor_10 (xor_10_out, undriven[9], or_1_out[9]);
  xor xor_11 (xor_11_out, undriven[10], or_1_out[10]);
  xor xor_12 (xor_12_out, undriven[11], or_1_out[11]);
  xor xor_13 (xor_13_out, undriven[12], or_1_out[12]);
  xor xor_14 (xor_14_out, undriven[13], or_1_out[13]);
  xor xor_15 (xor_15_out, undriven[14], or_1_out[14]);
  xor xor_16 (xor_16_out, undriven[15], or_1_out[15]);
  xor xor_17 (xor_17_out, xor_1_out, 1'b0);
  and and_65 (and_65_out, xor_1_out, 1'b0);
  and and_66 (and_66_out, undriven[0], or_1_out[0]);
  xor xor_18 (xor_18_out, xor_2_out, or_17_out);
  and and_67 (and_67_out, xor_2_out, or_17_out);
  and and_68 (and_68_out, undriven[1], or_1_out[1]);
  xor xor_19 (xor_19_out, xor_3_out, or_18_out);
  and and_69 (and_69_out, xor_3_out, or_18_out);
  and and_70 (and_70_out, undriven[2], or_1_out[2]);
  xor xor_20 (xor_20_out, xor_4_out, or_19_out);
  and and_71 (and_71_out, xor_4_out, or_19_out);
  and and_72 (and_72_out, undriven[3], or_1_out[3]);
  xor xor_21 (xor_21_out, xor_5_out, or_20_out);
  and and_73 (and_73_out, xor_5_out, or_20_out);
  and and_74 (and_74_out, undriven[4], or_1_out[4]);
  xor xor_22 (xor_22_out, xor_6_out, or_21_out);
  and and_75 (and_75_out, xor_6_out, or_21_out);
  and and_76 (and_76_out, undriven[5], or_1_out[5]);
  xor xor_23 (xor_23_out, xor_7_out, or_22_out);
  and and_77 (and_77_out, xor_7_out, or_22_out);
  and and_78 (and_78_out, undriven[6], or_1_out[6]);
  xor xor_24 (xor_24_out, xor_8_out, or_23_out);
  and and_79 (and_79_out, xor_8_out, or_23_out);
  and and_80 (and_80_out, undriven[7], or_1_out[7]);
  xor xor_25 (xor_25_out, xor_9_out, or_24_out);
  and and_81 (and_81_out, xor_9_out, or_24_out);
  and and_82 (and_82_out, undriven[8], or_1_out[8]);
  xor xor_26 (xor_26_out, xor_10_out, or_25_out);
  and and_83 (and_83_out, xor_10_out, or_25_out);
  and and_84 (and_84_out, undriven[9], or_1_out[9]);
  xor xor_27 (xor_27_out, xor_11_out, or_26_out);
  and and_85 (and_85_out, xor_11_out, or_26_out);
  and and_86 (and_86_out, undriven[10], or_1_out[10]);
  xor xor_28 (xor_28_out, xor_12_out, or_27_out);
  and and_87 (and_87_out, xor_12_out, or_27_out);
  and and_88 (and_88_out, undriven[11], or_1_out[11]);
  xor xor_29 (xor_29_out, xor_13_out, or_28_out);
  and and_89 (and_89_out, xor_13_out, or_28_out);
  and and_90 (and_90_out, undriven[12], or_1_out[12]);
  xor xor_30 (xor_30_out, xor_14_out, or_29_out);
  and and_91 (and_91_out, xor_14_out, or_29_out);
  and and_92 (and_92_out, undriven[13], or_1_out[13]);
  xor xor_31 (xor_31_out, xor_15_out, or_30_out);
  and and_93 (and_93_out, xor_15_out, or_30_out);
  and and_94 (and_94_out, undriven[14], or_1_out[14]);
  xor xor_32 (xor_32_out, xor_16_out, or_31_out);
  and and_95 (and_95_out, xor_16_out, or_31_out);
  and and_96 (and_96_out, undriven[15], or_1_out[15]);
  or or_17 (or_17_out, and_65_out, and_66_out);
  or or_18 (or_18_out, and_67_out, and_68_out);
  or or_19 (or_19_out, and_69_out, and_70_out);
  or or_20 (or_20_out, and_71_out, and_72_out);
  or or_21 (or_21_out, and_73_out, and_74_out);
  or or_22 (or_22_out, and_75_out, and_76_out);
  or or_23 (or_23_out, and_77_out, and_78_out);
  or or_24 (or_24_out, and_79_out, and_80_out);
  or or_25 (or_25_out, and_81_out, and_82_out);
  or or_26 (or_26_out, and_83_out, and_84_out);
  or or_27 (or_27_out, and_85_out, and_86_out);
  or or_28 (or_28_out, and_87_out, and_88_out);
  or or_29 (or_29_out, and_89_out, and_90_out);
  or or_30 (or_30_out, and_91_out, and_92_out);
  or or_31 (or_31_out, and_93_out, and_94_out);
  or or_32 (or_32_out, and_95_out, and_96_out);
  not not_35 (not_35_out, in_1[1]);
  not not_36 (not_36_out, not_35_out);
  not not_37 (not_37_out, not_35_out);
  not not_38 (not_38_out, not_35_out);
  not not_39 (not_39_out, not_35_out);
  not not_40 (not_40_out, not_35_out);
  not not_41 (not_41_out, not_35_out);
  not not_42 (not_42_out, not_35_out);
  not not_43 (not_43_out, not_35_out);
  not not_44 (not_44_out, not_35_out);
  not not_45 (not_45_out, not_35_out);
  not not_46 (not_46_out, not_35_out);
  not not_47 (not_47_out, not_35_out);
  not not_48 (not_48_out, not_35_out);
  not not_49 (not_49_out, not_35_out);
  not not_50 (not_50_out, not_35_out);
  not not_51 (not_51_out, not_35_out);
  and and_97 (and_97_out, xor_17_out, not_36_out);
  and and_98 (and_98_out, and_49_out[0], not_35_out);
  and and_99 (and_99_out, xor_18_out, not_37_out);
  and and_100 (and_100_out, and_49_out[1], not_35_out);
  and and_101 (and_101_out, xor_19_out, not_38_out);
  and and_102 (and_102_out, and_49_out[2], not_35_out);
  and and_103 (and_103_out, xor_20_out, not_39_out);
  and and_104 (and_104_out, and_49_out[3], not_35_out);
  and and_105 (and_105_out, xor_21_out, not_40_out);
  and and_106 (and_106_out, and_49_out[4], not_35_out);
  and and_107 (and_107_out, xor_22_out, not_41_out);
  and and_108 (and_108_out, and_49_out[5], not_35_out);
  and and_109 (and_109_out, xor_23_out, not_42_out);
  and and_110 (and_110_out, and_49_out[6], not_35_out);
  and and_111 (and_111_out, xor_24_out, not_43_out);
  and and_112 (and_112_out, and_49_out[7], not_35_out);
  and and_113 (and_113_out, xor_25_out, not_44_out);
  and and_114 (and_114_out, and_49_out[8], not_35_out);
  and and_115 (and_115_out, xor_26_out, not_45_out);
  and and_116 (and_116_out, and_49_out[9], not_35_out);
  and and_117 (and_117_out, xor_27_out, not_46_out);
  and and_118 (and_118_out, and_49_out[10], not_35_out);
  and and_119 (and_119_out, xor_28_out, not_47_out);
  and and_120 (and_120_out, and_49_out[11], not_35_out);
  and and_121 (and_121_out, xor_29_out, not_48_out);
  and and_122 (and_122_out, and_49_out[12], not_35_out);
  and and_123 (and_123_out, xor_30_out, not_49_out);
  and and_124 (and_124_out, and_49_out[13], not_35_out);
  and and_125 (and_125_out, xor_31_out, not_50_out);
  and and_126 (and_126_out, and_49_out[14], not_35_out);
  and and_127 (and_127_out, xor_32_out, not_51_out);
  and and_128 (and_128_out, and_49_out[15], not_35_out);
  or or_33 (or_33_out, and_97_out, and_98_out);
  or or_34 (or_34_out, and_99_out, and_100_out);
  or or_35 (or_35_out, and_101_out, and_102_out);
  or or_36 (or_36_out, and_103_out, and_104_out);
  or or_37 (or_37_out, and_105_out, and_106_out);
  or or_38 (or_38_out, and_107_out, and_108_out);
  or or_39 (or_39_out, and_109_out, and_110_out);
  or or_40 (or_40_out, and_111_out, and_112_out);
  or or_41 (or_41_out, and_113_out, and_114_out);
  or or_42 (or_42_out, and_115_out, and_116_out);
  or or_43 (or_43_out, and_117_out, and_118_out);
  or or_44 (or_44_out, and_119_out, and_120_out);
  or or_45 (or_45_out, and_121_out, and_122_out);
  or or_46 (or_46_out, and_123_out, and_124_out);
  or or_47 (or_47_out, and_125_out, and_126_out);
  or or_48 (or_48_out, and_127_out, and_128_out);
  not not_52 (not_52_out, or_33_out);
  not not_53 (not_53_out, or_34_out);
  not not_54 (not_54_out, or_35_out);
  not not_55 (not_55_out, or_36_out);
  not not_56 (not_56_out, or_37_out);
  not not_57 (not_57_out, or_38_out);
  not not_58 (not_58_out, or_39_out);
  not not_59 (not_59_out, or_40_out);
  not not_60 (not_60_out, or_41_out);
  not not_61 (not_61_out, or_42_out);
  not not_62 (not_62_out, or_43_out);
  not not_63 (not_63_out, or_44_out);
  not not_64 (not_64_out, or_45_out);
  not not_65 (not_65_out, or_46_out);
  not not_66 (not_66_out, or_47_out);
  not not_67 (not_67_out, or_48_out);
  not not_68 (not_68_out, in_1[0]);
  not not_69 (not_69_out, in_1[0]);
  not not_70 (not_70_out, in_1[0]);
  not not_71 (not_71_out, in_1[0]);
  not not_72 (not_72_out, in_1[0]);
  not not_73 (not_73_out, in_1[0]);
  not not_74 (not_74_out, in_1[0]);
  not not_75 (not_75_out, in_1[0]);
  not not_76 (not_76_out, in_1[0]);
  not not_77 (not_77_out, in_1[0]);
  not not_78 (not_78_out, in_1[0]);
  not not_79 (not_79_out, in_1[0]);
  not not_80 (not_80_out, in_1[0]);
  not not_81 (not_81_out, in_1[0]);
  not not_82 (not_82_out, in_1[0]);
  not not_83 (not_83_out, in_1[0]);
  and and_129 (and_129_out, or_33_out, not_68_out);
  and and_130 (and_130_out, not_52_out, in_1[0]);
  and and_131 (and_131_out, or_34_out, not_69_out);
  and and_132 (and_132_out, not_53_out, in_1[0]);
  and and_133 (and_133_out, or_35_out, not_70_out);
  and and_134 (and_134_out, not_54_out, in_1[0]);
  and and_135 (and_135_out, or_36_out, not_71_out);
  and and_136 (and_136_out, not_55_out, in_1[0]);
  and and_137 (and_137_out, or_37_out, not_72_out);
  and and_138 (and_138_out, not_56_out, in_1[0]);
  and and_139 (and_139_out, or_38_out, not_73_out);
  and and_140 (and_140_out, not_57_out, in_1[0]);
  and and_141 (and_141_out, or_39_out, not_74_out);
  and and_142 (and_142_out, not_58_out, in_1[0]);
  and and_143 (and_143_out, or_40_out, not_75_out);
  and and_144 (and_144_out, not_59_out, in_1[0]);
  and and_145 (and_145_out, or_41_out, not_76_out);
  and and_146 (and_146_out, not_60_out, in_1[0]);
  and and_147 (and_147_out, or_42_out, not_77_out);
  and and_148 (and_148_out, not_61_out, in_1[0]);
  and and_149 (and_149_out, or_43_out, not_78_out);
  and and_150 (and_150_out, not_62_out, in_1[0]);
  and and_151 (and_151_out, or_44_out, not_79_out);
  and and_152 (and_152_out, not_63_out, in_1[0]);
  and and_153 (and_153_out, or_45_out, not_80_out);
  and and_154 (and_154_out, not_64_out, in_1[0]);
  and and_155 (and_155_out, or_46_out, not_81_out);
  and and_156 (and_156_out, not_65_out, in_1[0]);
  and and_157 (and_157_out, or_47_out, not_82_out);
  and and_158 (and_158_out, not_66_out, in_1[0]);
  and and_159 (and_159_out, or_48_out, not_83_out);
  and and_160 (and_160_out, not_67_out, in_1[0]);
  or or_49 (out_4[0], and_129_out, and_130_out);
  or or_50 (out_4[1], and_131_out, and_132_out);
  or or_51 (out_4[2], and_133_out, and_134_out);
  or or_52 (out_4[3], and_135_out, and_136_out);
  or or_53 (out_4[4], and_137_out, and_138_out);
  or or_54 (out_4[5], and_139_out, and_140_out);
  or or_55 (out_4[6], and_141_out, and_142_out);
  or or_56 (out_4[7], and_143_out, and_144_out);
  or or_57 (out_4[8], and_145_out, and_146_out);
  or or_58 (out_4[9], and_147_out, and_148_out);
  or or_59 (out_4[10], and_149_out, and_150_out);
  or or_60 (out_4[11], and_151_out, and_152_out);
  or or_61 (out_4[12], and_153_out, and_154_out);
  or or_62 (out_4[13], and_155_out, and_156_out);
  or or_63 (out_4[14], and_157_out, and_158_out);
  or or_64 (out_4[15], and_159_out, and_160_out);
  // Probe on out_4

  // Other names for the same wires on the sheet: result[15:0] = out_4
endmodule
