// Logisim project computer.circ as structural Verilog: 3 circuits, main circuit Computer
module Computer (
  input  in_1,
  input  in_2,
  input  in_3,
  input  reset
);

  wire and_1_out, and_2_out, and_3_out, and_4_out, and_5_out, and_6_out, and_7_out, and_8_out, clock_1_out,
       clock_2_out, comparator_1_gt, comparator_2_lt, not_1_out, not_2_out, not_3_out, or_1_out, or_2_out,
       or_3_out, or_4_out, rgb_video_1_p3;
  wire [2:2] rgb_video_1_p6;
  wire [7:0] rgb_video_1_p4, rgb_video_2_p4;
  wire [14:0] A_q, adder_1_out, divider_1_rem, register_1_q, rgb_video_1_p5, shifter_1_out, subtractor_1_out;
  wire [15:0] alu_c_1_outp, D_q, multiplexer_1_out, multiplexer_2_out, mycounter_1_outp, mycounter_2_outp,
       ram_1_dout, register_2_q, rom_1_data;
  wire [15:15] A_q_2;

  ROM #(.addrWidth(15), .dataWidth(16)) rom_1 (.addr(mycounter_1_outp[14:0]), .data(rom_1_data));
  Clock #(.highDuration(2), .lowDuration(2)) clock_1 (.out(clock_1_out));
  Clock clock_2 (.out(clock_2_out));
  and and_1 (and_1_out, rom_1_data[3], rom_1_data[15]);
  // Probe on rom_1_data
  not not_1 (not_1_out, rom_1_data[15]);
  Multiplexer #(.width(16)) multiplexer_1 (
    .in0(alu_c_1_outp), .in1(rom_1_data), .out(multiplexer_1_out), .sel(not_1_out));
  and and_2 (and_2_out, rom_1_data[4], rom_1_data[15]);
  or or_1 (or_1_out, rom_1_data[5], not_1_out);
  Register #(.width(16)) A (.D(multiplexer_1_out), .en(or_1_out), .clk(clock_1_out), .Q({A_q_2[15], A_q}), .clr(in_3));
  // RGB_Video #(.cursor("No Cursor"), .height(256), .scale(1), .width(256)) rgb_video_1: pin names not known; wires that end beside it: reset, clock_2_out, rgb_video_1_p3, rgb_video_1_p4, rgb_video_1_p5[7:0], {rgb_video_1_p6[2], 1'b0, rgb_video_1_p6[2]}
  Register #(.width(16)) D (.D(alu_c_1_outp), .en(and_2_out), .clk(clock_1_out), .Q(D_q), .clr(in_2));
  and and_3 (and_3_out, rom_1_data[15], or_4_out);
  Multiplexer #(.width(16)) multiplexer_2 (
    .in0({A_q_2[15], A_q}), .in1(ram_1_dout), .out(multiplexer_2_out), .sel(rom_1_data[12]));
  // RGB_Video #(.cursor("No Cursor"), .height(256), .scale(1), .width(256)) rgb_video_2: pin names not known; wires that end beside it: reset, clock_2_out, adder_1_out[8], rgb_video_2_p4, rgb_video_1_p5[7:0], {rgb_video_1_p6[2], 1'b0, rgb_video_1_p6[2]}
  or or_2 (or_2_out, reset, mycounter_2_outp[4]);
  myCounter mycounter_1 (
    .clock(clock_1_out), .inc(1'b1), .reset(reset), .load(and_3_out), .inp({A_q_2[15], A_q}),
    .outp(mycounter_1_outp));
  // Probe on mycounter_1_outp
  ALU_C alu_c_1 (.control(rom_1_data[11:6]), .x(D_q), .y(multiplexer_2_out), .outp(alu_c_1_outp));
  and and_4 (and_4_out, or_3_out, not_2_out);
  not not_2 (not_2_out, alu_c_1_outp[15]);
  not not_3 (not_3_out, or_3_out);
  and and_5 (and_5_out, not_3_out, rom_1_data[1]);
  and and_6 (and_6_out, alu_c_1_outp[15], rom_1_data[2]);
  myCounter mycounter_2 (
    .clock(clock_2_out), .inc(1'b1), .reset(or_2_out), .outp(mycounter_2_outp));  // open: load, inp
  and and_7 (and_7_out, and_4_out, rom_1_data[0]);
  Subtractor #(.width(15)) subtractor_1 (.a(register_1_q), .b(15'h4000), .out(subtractor_1_out));  // open: bin, bout
  Divider #(.width(15)) divider_1 (.a(subtractor_1_out), .b(15'h20), .rem(divider_1_rem));  // open: out, upper
  or or_3 (or_3_out, alu_c_1_outp[15], alu_c_1_outp[14], alu_c_1_outp[13], alu_c_1_outp[12], alu_c_1_outp[11], alu_c_1_outp[10], alu_c_1_outp[9], alu_c_1_outp[8], alu_c_1_outp[7], alu_c_1_outp[6], alu_c_1_outp[5], alu_c_1_outp[4], alu_c_1_outp[3], alu_c_1_outp[2], alu_c_1_outp[1], alu_c_1_outp[0]);
  or or_4 (or_4_out, and_7_out, and_5_out, and_6_out);
  Comparator #(.mode("unsigned"), .width(15)) comparator_1 (
    .a(A_q), .b(15'h3fff), .gt(comparator_1_gt));  // open: eq, lt
  Comparator #(.mode("unsigned"), .width(15)) comparator_2 (
    .a(A_q), .b(15'h6000), .lt(comparator_2_lt));  // open: gt, eq
  Divider #(.width(15)) divider_2 (.a(subtractor_1_out), .b(15'h20), .out(rgb_video_1_p5));  // open: upper, rem
  Shifter #(.width(15)) shifter_1 (.in(divider_1_rem), .\dist (4'b0100), .out(shifter_1_out));
  and and_8 (and_8_out, comparator_1_gt, and_1_out, comparator_2_lt);
  Adder #(.width(15)) adder_1 (.a(shifter_1_out), .b(mycounter_2_outp[14:0]), .out(adder_1_out));  // open: cin, cout
  not not_4 (rgb_video_1_p3, adder_1_out[8]);
  Register #(.width(15)) register_1 (.D(A_q), .en(and_8_out), .clk(clock_2_out), .Q(register_1_q), .clr(reset));
  Demultiplexer #(.width(8)) demultiplexer_1 (
    .out0(rgb_video_1_p4), .out1(rgb_video_2_p4), .in(adder_1_out[7:0]), .sel(adder_1_out[8]));
  RAM #(.addrWidth(15), .asyncread("true"), .clearpin("true"), .dataWidth(16)) ram_1 (
    .addr(A_q), .we(and_1_out), .oe(1'b1), .clk(clock_1_out), .din(alu_c_1_outp), .dout(ram_1_dout),
    .clr(in_1));
  Multiplexer #(.select(4)) multiplexer_3 (
    .in0(register_2_q[0]), .in1(register_2_q[1]), .in2(register_2_q[2]), .in3(register_2_q[3]),
    .in4(register_2_q[4]), .in5(register_2_q[5]), .in6(register_2_q[6]), .in7(register_2_q[7]),
    .in8(register_2_q[8]), .in9(register_2_q[9]), .in10(register_2_q[10]), .in11(register_2_q[11]),
    .in12(register_2_q[12]), .in13(register_2_q[13]), .in14(register_2_q[14]), .in15(register_2_q[15]),
    .out(rgb_video_1_p6[2]), .sel(mycounter_2_outp[3:0]));
  Register #(.width(16)) register_2 (.D(ram_1_dout), .en(and_8_out), .clk(clock_2_out), .Q(register_2_q), .clr(reset));

  // Notes on the sheet:
  //   contents of rom_1 (hex, n*v repeats v):
  //   0 fc10 17 e306 10 e308 4000 ec10 11 e308 11 fc20 ee88 11 fc10 20 e090 11 e308 10 fc98 a e301 17 ea87
endmodule

module Computer_C (
  input  reset
);

  wire clock_1_out, cpu_1_writem;
  wire [14:0] cpu_1_addressm, cpu_1_pc;
  wire [15:0] cpu_1_outm, ram_1_dout, rom_1_data;

  ROM #(.addrWidth(15), .dataWidth(16)) rom_1 (.addr(cpu_1_pc), .data(rom_1_data));
  Clock clock_1 (.out(clock_1_out));
  CPU cpu_1 (
    .clock(clock_1_out), .instruction(rom_1_data), .inM(ram_1_dout), .reset(reset), .writeM(cpu_1_writem),
    .outM(cpu_1_outm), .addressM(cpu_1_addressm), .pc(cpu_1_pc));
  RAM #(.addrWidth(15), .dataWidth(16)) ram_1 (
    .addr(cpu_1_addressm), .we(cpu_1_writem), .oe(1'b1), .clk(clock_1_out), .din(cpu_1_outm),
    .dout(ram_1_dout));

  // Notes on the sheet:
  //   contents of rom_1 (hex, n*v repeats v):
  //   7*3030 3130 d0a 3131 3130 3131 3030 3030 3031 3030 3030 d0a 7*3030 3131 d0a 3131 3130 3030 3030 3130
  //   3031 3030 3030 d0a 8*3030 d0a 3131 3130 3030 3131 3030 3030 3130 3030 d0a
endmodule

module CPU (
  input  clock,
  input  [15:0] instruction,
  input  [15:0] inM,
  input  reset,
  output writeM,
  output [15:0] outM,
  output [14:0] addressM,
  output [14:0] pc
);

  wire and_1_out, and_2_out, and_3_out, and_4_out, mycounter_1_p3, not_1_out, not_2_out, not_3_out, or_1_out,
       or_2_out;
  wire [15:0] D_q, multiplexer_1_out, multiplexer_2_out;
  wire [15:15] A_q, mycounter_1_p5;

  not not_1 (not_1_out, instruction[15]);
  Multiplexer #(.width(16)) multiplexer_1 (.in0(outM), .in1(instruction), .out(multiplexer_1_out), .sel(not_1_out));
  or or_1 (or_1_out, instruction[5], not_1_out);
  Register #(.width(16)) A (.D(multiplexer_1_out), .en(or_1_out), .clk(clock), .Q({A_q[15], addressM}));  // open: clr
  Register #(.width(16)) D (.D(outM), .en(instruction[4]), .clk(clock), .Q(D_q));  // open: clr
  Multiplexer #(.width(16)) multiplexer_2 (
    .in0({A_q[15], addressM}), .in1(inM), .out(multiplexer_2_out), .sel(instruction[12]));
  // myCounter mycounter_1: pin names not known; wires that end beside it: 1'b1, reset, mycounter_1_p3, {A_q[15], addressM}, {mycounter_1_p5[15], pc}
  ALU_C alu_c_1 (.control(instruction[11:6]), .x(D_q), .y(multiplexer_2_out), .outp(outM));
  not not_2 (not_2_out, outM[15]);
  and and_1 (and_1_out, or_2_out, not_2_out);
  not not_3 (not_3_out, or_2_out);
  and and_2 (and_2_out, not_3_out, instruction[1]);
  and and_3 (and_3_out, outM[15], instruction[2]);
  and and_4 (and_4_out, and_1_out, instruction[0]);
  or or_2 (or_2_out, outM[15], outM[14], outM[13], outM[12], outM[11], outM[10], outM[9], outM[8], outM[7], outM[6], outM[5], outM[4], outM[3], outM[2], outM[1], outM[0]);
  or or_3 (mycounter_1_p3, and_4_out, and_2_out, and_3_out);

  assign writeM = instruction[3];
endmodule
