// Logisim project sequential_logic.circ as structural Verilog: 4 circuits, main circuit myBit
module myBit (
  input  in_1,
  input  in_2,
  output out_3
);

  wire clock_1_out, multiplexer_1_out;

  Clock clock_1 (.out(clock_1_out));
  Multiplexer multiplexer_1 (.in0(out_3), .in1(in_2), .out(multiplexer_1_out), .sel(in_1));
  D_Flip_Flop d_ff_1 (.D(multiplexer_1_out), .clk(clock_1_out), .Q(out_3));  // open: Qn, preset, reset
endmodule

module myRegister (
  input  in_1,
  input  [15:0] inp,
  output [15:0] out_3
);

  wire clock_1_out, multiplexer_1_out, multiplexer_2_out, multiplexer_3_out, multiplexer_4_out,
       multiplexer_5_out, multiplexer_6_out, multiplexer_7_out, multiplexer_8_out, multiplexer_9_out,
       multiplexer_10_out, multiplexer_11_out, multiplexer_12_out, multiplexer_13_out, multiplexer_14_out,
       multiplexer_15_out, multiplexer_16_out;

  Clock clock_1 (.out(clock_1_out));
  Multiplexer multiplexer_1 (.in0(out_3[0]), .in1(inp[0]), .out(multiplexer_1_out), .sel(in_1));
  Multiplexer multiplexer_2 (.in0(out_3[1]), .in1(inp[1]), .out(multiplexer_2_out), .sel(in_1));
  Multiplexer multiplexer_3 (.in0(out_3[2]), .in1(inp[2]), .out(multiplexer_3_out), .sel(in_1));
  Multiplexer multiplexer_4 (.in0(out_3[3]), .in1(inp[3]), .out(multiplexer_4_out), .sel(in_1));
  Multiplexer multiplexer_5 (.in0(out_3[4]), .in1(inp[4]), .out(multiplexer_5_out), .sel(in_1));
  Multiplexer multiplexer_6 (.in0(out_3[5]), .in1(inp[5]), .out(multiplexer_6_out), .sel(in_1));
  Multiplexer multiplexer_7 (.in0(out_3[6]), .in1(inp[6]), .out(multiplexer_7_out), .sel(in_1));
  Multiplexer multiplexer_8 (.in0(out_3[7]), .in1(inp[7]), .out(multiplexer_8_out), .sel(in_1));
  Multiplexer multiplexer_9 (.in0(out_3[8]), .in1(inp[8]), .out(multiplexer_9_out), .sel(in_1));
  Multiplexer multiplexer_10 (.in0(out_3[9]), .in1(inp[9]), .out(multiplexer_10_out), .sel(in_1));
  Multiplexer multiplexer_11 (.in0(out_3[10]), .in1(inp[10]), .out(multiplexer_11_out), .sel(in_1));
  Multiplexer multiplexer_12 (.in0(out_3[11]), .in1(inp[11]), .out(multiplexer_12_out), .sel(in_1));
  Multiplexer multiplexer_13 (.in0(out_3[12]), .in1(inp[12]), .out(multiplexer_13_out), .sel(in_1));
  Multiplexer multiplexer_14 (.in0(out_3[13]), .in1(inp[13]), .out(multiplexer_14_out), .sel(in_1));
  Multiplexer multiplexer_15 (.in0(out_3[14]), .in1(inp[14]), .out(multiplexer_15_out), .sel(in_1));
  Multiplexer multiplexer_16 (.in0(out_3[15]), .in1(inp[15]), .out(multiplexer_16_out), .sel(in_1));
  D_Flip_Flop d_ff_1 (.D(multiplexer_1_out), .clk(clock_1_out), .Q(out_3[0]));  // open: Qn, preset, reset
  D_Flip_Flop d_ff_2 (.D(multiplexer_2_out), .clk(clock_1_out), .Q(out_3[1]));  // open: Qn, preset, reset
  D_Flip_Flop d_ff_3 (.D(multiplexer_3_out), .clk(clock_1_out), .Q(out_3[2]));  // open: Qn, preset, reset
  D_Flip_Flop d_ff_4 (.D(multiplexer_4_out), .clk(clock_1_out), .Q(out_3[3]));  // open: Qn, preset, reset
  D_Flip_Flop d_ff_5 (.D(multiplexer_5_out), .clk(clock_1_out), .Q(out_3[4]));  // open: Qn, preset, reset
  D_Flip_Flop d_ff_6 (.D(multiplexer_6_out), .clk(clock_1_out), .Q(out_3[5]));  // open: Qn, preset, reset
  D_Flip_Flop d_ff_7 (.D(multiplexer_7_out), .clk(clock_1_out), .Q(out_3[6]));  // open: Qn, preset, reset
  D_Flip_Flop d_ff_8 (.D(multiplexer_8_out), .clk(clock_1_out), .Q(out_3[7]));  // open: Qn, preset, reset
  D_Flip_Flop d_ff_9 (.D(multiplexer_9_out), .clk(clock_1_out), .Q(out_3[8]));  // open: Qn, preset, reset
  D_Flip_Flop d_ff_10 (.D(multiplexer_10_out), .clk(clock_1_out), .Q(out_3[9]));  // open: Qn, preset, reset
  D_Flip_Flop d_ff_11 (.D(multiplexer_11_out), .clk(clock_1_out), .Q(out_3[10]));  // open: Qn, preset, reset
  D_Flip_Flop d_ff_12 (.D(multiplexer_12_out), .clk(clock_1_out), .Q(out_3[11]));  // open: Qn, preset, reset
  D_Flip_Flop d_ff_13 (.D(multiplexer_13_out), .clk(clock_1_out), .Q(out_3[12]));  // open: Qn, preset, reset
  D_Flip_Flop d_ff_14 (.D(multiplexer_14_out), .clk(clock_1_out), .Q(out_3[13]));  // open: Qn, preset, reset
  D_Flip_Flop d_ff_15 (.D(multiplexer_15_out), .clk(clock_1_out), .Q(out_3[14]));  // open: Qn, preset, reset
  D_Flip_Flop d_ff_16 (.D(multiplexer_16_out), .clk(clock_1_out), .Q(out_3[15]));  // open: Qn, preset, reset
endmodule

module RAM8 (
  input  [15:0] value,
  input  load,
  input  [2:0] Address,
  output [15:0] out_4
);

  wire clock_1_out, demultiplexer_1_out0, demultiplexer_1_out1, demultiplexer_1_out2, demultiplexer_1_out3,
       demultiplexer_1_out4, demultiplexer_1_out5, demultiplexer_1_out6, demultiplexer_1_out7;
  wire [15:0] register_1_q, register_2_q, register_3_q, register_4_q, register_5_q, register_6_q,
       register_7_q, register_8_q;

  Demultiplexer #(.select(3)) demultiplexer_1 (
    .out0(demultiplexer_1_out0), .out1(demultiplexer_1_out1), .out2(demultiplexer_1_out2),
    .out3(demultiplexer_1_out3), .out4(demultiplexer_1_out4), .out5(demultiplexer_1_out5),
    .out6(demultiplexer_1_out6), .out7(demultiplexer_1_out7), .in(load), .sel(Address));
  Clock clock_1 (.out(clock_1_out));
  Register #(.width(16)) register_1 (
    .D(value), .en(demultiplexer_1_out0), .clk(clock_1_out), .Q(register_1_q));  // open: clr
  Register #(.width(16)) register_2 (
    .D(value), .en(demultiplexer_1_out1), .clk(clock_1_out), .Q(register_2_q));  // open: clr
  Register #(.width(16)) register_3 (
    .D(value), .en(demultiplexer_1_out2), .clk(clock_1_out), .Q(register_3_q));  // open: clr
  Register #(.width(16)) register_4 (
    .D(value), .en(demultiplexer_1_out3), .clk(clock_1_out), .Q(register_4_q));  // open: clr
  Register #(.width(16)) register_5 (
    .D(value), .en(demultiplexer_1_out4), .clk(clock_1_out), .Q(register_5_q));  // open: clr
  Register #(.width(16)) register_6 (
    .D(value), .en(demultiplexer_1_out5), .clk(clock_1_out), .Q(register_6_q));  // open: clr
  Register #(.width(16)) register_7 (
    .D(value), .en(demultiplexer_1_out6), .clk(clock_1_out), .Q(register_7_q));  // open: clr
  Register #(.width(16)) register_8 (
    .D(value), .en(demultiplexer_1_out7), .clk(clock_1_out), .Q(register_8_q));  // open: clr
  Multiplexer #(.select(3), .width(16)) multiplexer_1 (
    .in0(register_1_q), .in1(register_2_q), .in2(register_3_q), .in3(register_4_q), .in4(register_5_q),
    .in5(register_6_q), .in6(register_7_q), .in7(register_8_q), .out(out_4), .sel(Address));
endmodule

module myCounter (
  input  clock,
  input  inc,
  input  reset,
  input  load,
  input  [15:0] inp,
  output [15:0] outp
);

  wire or_1_out;
  wire [15:0] inc16_1_outp, multiplexer_1_out;

  or or_1 (or_1_out, load, inc);
  Multiplexer #(.width(16)) multiplexer_1 (.in0(inc16_1_outp), .in1(inp), .out(multiplexer_1_out), .sel(load));
  Register #(.width(16)) register_1 (.D(multiplexer_1_out), .en(or_1_out), .clk(clock), .Q(outp), .clr(reset));
  Inc16 inc16_1 (.inp(outp), .outp(inc16_1_outp));
endmodule
